# Fritzing sketch v1 (saved by Fritzing 0.9.3b)
circuit board: 9cm x 5.4cm

parts:
  PW1 = Power plug
  S1 = Toggle Switch [package=THT]
  PP1 = female pin header, 5 pins [form="♀ (female)"]
  LM7805 = Voltage Regulator - 5V [package="TO220 [THT]"]
  100μF = Electrolytic Capacitor [capacitance=100μF package="100 mil [THT, electrolytic]"]
  12v+ = female pin header, 5 pins [form="♀ (female)"]
  12v- = female pin header, 5 pins [form="♀ (female)"]
  5v- = female pin header, 5 pins [form="♀ (female)"]
  +1 = Rectifier Diode [part_number=1N4001 package="300 mil [THT]"]
  1K1 = Resistor [tolerance=±5% resistance=220 package=THT]
  1 = LED - 3mm [color="Red (633nm)" package="3 mm [THT]"]
  LDR1 = Capacitor [package=cap-pth-small-kit]
  100k1 = Resistor [tolerance=±5% resistance=220 package=THT]
  0_1u1 = Ceramic Capacitor [capacitance=100nF package="100 mil [THT, multilayer]"]
  Atmega328P1 = atmega328 [package=dip]
  10K1 = Resistor [tolerance=±5% resistance=220 package=THT]
  XL1 = CRYSTAL - kHz [frequency="16 Mhz"]
  2 = LED - 3mm [color="Red (633nm)" package="3 mm [THT]"]
  22p1 = Capacitor [package=cap-pth-small-kit]
  22p2 = Capacitor [package=cap-pth-small-kit]
  -_+1 = Rectifier Diode [part_number=1N4001 package="300 mil [THT]"]
  RGB1 = RGB LED - (4 legs) [package="5 mm [THT]"]
  1K2 = Resistor [tolerance=±5% resistance=220 package=THT]
  +5V1 = Battery

nets:
  GND: PW1.GND, LM7805.GND, 100μF.-, 12v-.pin1, 12v-.pin2, 12v-.pin3, 12v-.pin4, 12v-.pin5, 5v-.pin1, 5v-.pin2, 5v-.pin3, 5v-.pin4, 5v-.pin5, 1K1.Pin_0, LDR1.2, Atmega328P1.GND, 2.cathode, 22p1.1, 22p2.1, +5V1.-
  N1: PW1.VCC, S1.L1
  N2: S1.COM, LM7805.input_voltage, 12v+.pin1, 12v+.pin2, 12v+.pin3, 12v+.pin4, 12v+.pin5
  N3: PP1.pin1, PP1.pin2, PP1.pin3, PP1.pin4, PP1.pin5, LM7805.output_voltage, 100μF.+, -_+1.anode, +5V1.+
  N4: +1.cathode, 1.anode, 100k1.Pin_0, Atmega328P1.VCC, Atmega328P1.AVCC, Atmega328P1.AREF, 10K1.Pin_0, -_+1.cathode
  N5: 1K1.Pin_1, 1.cathode
  N6: LDR1.1, 100k1.Pin_1
  N7: 0_1u1.0, Atmega328P1.RESET, 10K1.Pin_1
  N8: Atmega328P1.XLAT1, XL1.pin_0, 22p1.2
  N9: Atmega328P1.XLAT2, XL1.pin_1, 22p2.2
  N10: Atmega328P1.D5_(PWM), RGB1.blue_cathode
  N11: Atmega328P1.D6_(PWM), RGB1.green_cathode
  N12: Atmega328P1.D7, RGB1.red_cathode
  N13: RGB1.common_anode, 1K2.Pin_0

notes:
  -
  -----
  ----- Ardu5 -----
  GND
  -1K-
  16Mhz
  GND +V  TX RX DTR
  +5V GND TX RX
  SDA
  SCL
  RX TX
  +5Vcc
  5´ 6´ 7  8
  RST 0  1  2  3´ 4  +  -
  13 12 11´10´ 9´ 8
  USB-Serial
  Bluetooth HC06
  arduino
  A5 A4 A3 A2 A1 A0
  7.-.6.5
  +12Vcc
  .
