# Fritzing sketch v4 (saved by Fritzing 0.9.3b)

parts:
  Switch = Toggle Switch [package=THT]
  1kΩ = Resistor [tolerance=±5% resistance=1k package=THT]
  In7v = Power plug
  GND = female pin header, 5 pins [form="♀ (female)"]
  5V = female pin header, 5 pins [form="♀ (female)"]
  LM7805 = Voltage Regulator - 5V [package="TO220 [THT]"]
  atmega328p = atmega328 [package=dip]
  C4 = Ceramic Capacitor [capacitance=10nF package="100 mil [THT, multilayer]"]
  22pF = Ceramic Capacitor [capacitance=22pF package="100 mil [THT, multilayer]"]
  RESET = Pushbutton [package="[THT]"]
  7v+ = female pin header, 5 pins [form="♀ (female)"]
  GND_2 = female pin header, 5 pins [form="♀ (female)"]
  220Ω = Resistor [tolerance=±5% resistance=220 package=THT]
  220Ω_2 = Resistor [tolerance=±5% resistance=220 package=THT]
  LED_ON = LED - 5mm [color="Red (633nm)" package="5 mm [THT]"]
  D0-D4 = female pin header, 5 pins [form="♀ (female)"]
  D5-D8 = female pin header, 5 pins [form="♀ (female)"]
  IN7V = female pin header, 2 pins [form="♀ (female)"]
  D9-D13 = female pin header, 5 pins [form="♀ (female)"]
  100nF = Electrolytic Capacitor [capacitance=100nF package="100 mil [THT, electrolytic]"]
  A0-A5 = female pin header, 6 pins [form="♀ (female)"]
  C3 = Electrolytic Capacitor [capacitance=22µF package="100 mil [THT, electrolytic]"]
  PIN_13 = LED - 5mm [color="Red (633nm)" package="5 mm [THT]"]
  22pF_2 = Ceramic Capacitor [capacitance=22pF package="100 mil [THT, multilayer]"]
  16MHz = Crystal [frequency="16 Mhz" package=THT]

nets:
  N1: Switch.L1, In7v.VCC, IN7V.pin1
  N2: Switch.COM, LM7805.input_voltage, 7v+.pin1, 7v+.pin2, 7v+.pin3, 7v+.pin4, 7v+.pin5, C3.+
  N3: 1kΩ.Pin_0, 5V.pin1, 5V.pin2, 5V.pin3, 5V.pin4, 5V.pin5, LM7805.output_voltage, atmega328p.VCC, atmega328p.AVCC, atmega328p.AREF, C4.1, 220Ω_2.Pin_0, 100nF.+
  N4: 1kΩ.Pin_1, 22pF.0, RESET.Pin_2
  GND: In7v.GND, GND.pin1, GND.pin2, GND.pin3, GND.pin4, GND.pin5, LM7805.GND, atmega328p.GND, C4.0, RESET.Pin_3, GND_2.pin1, GND_2.pin2, GND_2.pin3, GND_2.pin4, GND_2.pin5, 220Ω.Pin_1, LED_ON.anode, IN7V.pin2, 100nF.-, C3.-, 22pF_2.0
  N5: atmega328p.D0_(RX), D0-D4.pin1
  N6: atmega328p.D1_(TX), D0-D4.pin2
  N7: atmega328p.D2, D0-D4.pin3
  N8: atmega328p.D3_(PWM), D0-D4.pin4
  N9: atmega328p.D4, D0-D4.pin5
  N10: atmega328p.XLAT1, 22pF.1, 16MHz.pin_0
  N11: atmega328p.XLAT2, D5-D8.pin1, 22pF_2.1, 16MHz.pin_1
  N12: atmega328p.D5_(PWM), D5-D8.pin2
  N13: atmega328p.D6_(PWM), D5-D8.pin3
  N14: atmega328p.D7, D5-D8.pin4
  N15: atmega328p.D8, D5-D8.pin5
  N16: atmega328p.D9_(PWM), D9-D13.pin1
  N17: atmega328p.D10_(PWM), D9-D13.pin2
  N18: atmega328p.D11_(PWM), D9-D13.pin3
  N19: atmega328p.D12, D9-D13.pin4
  N20: atmega328p.D13, D9-D13.pin5, PIN_13.anode
  N21: atmega328p.A0, A0-A5.pin1
  N22: atmega328p.A1, A0-A5.pin2
  N23: atmega328p.A2, A0-A5.pin3
  N24: atmega328p.A3, A0-A5.pin4
  N25: atmega328p.A4, A0-A5.pin5
  N26: atmega328p.A5, A0-A5.pin6
  N27: 220Ω.Pin_0, PIN_13.cathode
  N28: 220Ω_2.Pin_1, LED_ON.cathode
