# Fritzing sketch v5 (saved by Fritzing 0.9.3b)

parts:
  U1 = atmega328 [package=dip]
  100nF = Ceramic Capacitor [capacitance=100nF package="100 mil [THT, multilayer]"]
  V1 = DC Power [voltage=5]
  XTAL1 = Crystal [frequency="16 Mhz" package=THT]
  680Ω = Resistor [tolerance=±5% resistance=680 package=THT]
  LED-PIN13 = LED - 5mm [color="White (4500K)" package="5 mm [THT]"]
  S4 = SWITCH-MOMENTARY-2 [package=tactile-pth]
  18pF = Ceramic Capacitor [capacitance=18pF package="100 mil [THT, multilayer]"]
  18pF1 = Ceramic Capacitor [capacitance=18pF package="100 mil [THT, multilayer]"]
  D0_(RX) = female pin header, 1 pin [form="♀ (female)"]
  D1_(TX) = female pin header, 1 pin [form="♀ (female)"]
  D2 = female pin header, 1 pin [form="♀ (female)"]
  D3_(PWM) = female pin header, 1 pin [form="♀ (female)"]
  D4 = female pin header, 1 pin [form="♀ (female)"]
  VIN = female pin header, 1 pin [form="♀ (female)"]
  GND = female pin header, 2 pins [form="♀ (female)"]
  RESET = female pin header, 1 pin [form="♀ (female)"]
  10K = Resistor [tolerance=±5% resistance=10k package=THT]
  A5/SCL = female pin header, 1 pin [form="♀ (female)"]
  A4/SDA = female pin header, 1 pin [form="♀ (female)"]
  A3 = female pin header, 1 pin [form="♀ (female)"]
  A2 = female pin header, 1 pin [form="♀ (female)"]
  A1 = female pin header, 1 pin [form="♀ (female)"]
  A0 = female pin header, 1 pin [form="♀ (female)"]
  D9_(PWM) = female pin header, 1 pin [form="♀ (female)"]
  D10_(PWM) = female pin header, 1 pin [form="♀ (female)"]
  D11_(PWM) = female pin header, 1 pin [form="♀ (female)"]
  D12 = female pin header, 1 pin [form="♀ (female)"]
  D13 = female pin header, 1 pin [form="♀ (female)"]
  D5_(PWM) = female pin header, 1 pin [form="♀ (female)"]
  D6_(PWM) = female pin header, 1 pin [form="♀ (female)"]
  D7 = female pin header, 1 pin [form="♀ (female)"]
  D8 = female pin header, 1 pin [form="♀ (female)"]

nets:
  N1: U1.RESET, S4.2, RESET.pin1, 10K.Pin_0
  N2: U1.D0_(RX), D0_(RX).pin1
  N3: U1.D1_(TX), D1_(TX).pin1
  N4: U1.D2, D2.pin1
  N5: U1.D3_(PWM), D3_(PWM).pin1
  N6: U1.D4, D4.pin1
  N7: U1.VCC, U1.AVCC, U1.AREF, 100nF.1, V1.V+, VIN.pin1, 10K.Pin_1
  N8: U1.GND#7, 100nF.0, V1.V-, S4.1, GND.pin1, GND.pin2
  N9: U1.XLAT1, XTAL1.pin_1, 18pF1.0
  N10: U1.XLAT2, XTAL1.pin_0, 18pF.0
  N11: U1.D5_(PWM), D5_(PWM).pin1
  N12: U1.D6_(PWM), D6_(PWM).pin1
  N13: U1.D7, D7.pin1
  N14: U1.D8, D8.pin1
  N15: U1.D9_(PWM), D9_(PWM).pin1
  N16: U1.D10_(PWM), D10_(PWM).pin1
  N17: U1.D11_(PWM), D11_(PWM).pin1
  N18: U1.D12, D12.pin1
  N19: U1.D13, 680Ω.Pin_1, D13.pin1
  N20: U1.GND#21, LED-PIN13.cathode, 18pF.1, 18pF1.1
  N21: U1.A0, A0.pin1
  N22: U1.A1, A1.pin1
  N23: U1.A2, A2.pin1
  N24: U1.A3, A3.pin1
  N25: U1.A4, A4/SDA.pin1
  N26: U1.A5, A5/SCL.pin1
  N27: 680Ω.Pin_0, LED-PIN13.anode
