# Fritzing sketch v6 (saved by Fritzing 0.9.3b)

parts:
  U1 = atmega328 [package=dip]
  100nF = Ceramic Capacitor [capacitance=100nF package="100 mil [THT, multilayer]"]
  V1 = DC Power [voltage=5]
  XTAL1 = Crystal [frequency="16 Mhz" package=THT]
  680Ω = Resistor [tolerance=±5% resistance=680 package=THT]
  LED-PIN13 = LED - 5mm [color="White (4500K)" package="5 mm [THT]"]
  S4 = SWITCH-MOMENTARY-2 [package=tactile-pth]
  18pF = Ceramic Capacitor [capacitance=18pF package="100 mil [THT, multilayer]"]
  18pF1 = Ceramic Capacitor [capacitance=18pF package="100 mil [THT, multilayer]"]
  D0_(RX) = female pin header, 1 pin [form="♀ (female)"]
  D1_(TX) = female pin header, 1 pin [form="♀ (female)"]
  D2 = female pin header, 1 pin [form="♀ (female)"]
  D3_(PWM) = female pin header, 1 pin [form="♀ (female)"]
  D4 = female pin header, 1 pin [form="♀ (female)"]
  VIN = female pin header, 1 pin [form="♀ (female)"]
  GND = female pin header, 2 pins [form="♀ (female)"]
  RESET = female pin header, 1 pin [form="♀ (female)"]
  10K = Resistor [tolerance=±5% resistance=10k package=THT]
  A5/SCL = female pin header, 1 pin [form="♀ (female)"]
  A4/SDA = female pin header, 1 pin [form="♀ (female)"]
  A3 = female pin header, 1 pin [form="♀ (female)"]
  A2 = female pin header, 1 pin [form="♀ (female)"]
  A1 = female pin header, 1 pin [form="♀ (female)"]
  A0 = female pin header, 1 pin [form="♀ (female)"]
  D9_(PWM) = female pin header, 1 pin [form="♀ (female)"]
  D10_(PWM) = female pin header, 1 pin [form="♀ (female)"]
  D11_(PWM) = female pin header, 1 pin [form="♀ (female)"]
  D12 = female pin header, 1 pin [form="♀ (female)"]
  D13 = female pin header, 1 pin [form="♀ (female)"]
  D5_(PWM) = female pin header, 1 pin [form="♀ (female)"]
  D6_(PWM) = female pin header, 1 pin [form="♀ (female)"]
  D7 = female pin header, 1 pin [form="♀ (female)"]
  D8 = female pin header, 1 pin [form="♀ (female)"]
  J1 = Power Jack [package=power_jack_pth]
  switch1 = SPST Switch [package=switch-spdt_lock.007s]
  ON_12v = LED - 5mm [color="Red (633nm)" package="5 mm [THT]"]
  R1 = Resistor [tolerance=±5% resistance=220 package=THT]
  IN_12v- = female pin header, 1 pin [form="♀ (female)"]
  IN_12v+ = female pin header, 1 pin [form="♀ (female)"]
  LM7805 = Voltage Regulator - 5V [package="TO220 [THT]"]
  C2 = Electrolytic Capacitor [capacitance=100µF package="100 mil [THT, electrolytic]"]
  IN_5v+ = female pin header, 1 pin [form="♀ (female)"]  # not connected
  IN_5v+1 = female pin header, 1 pin [form="♀ (female)"]
  R3 = Resistor [tolerance=±5% resistance=270 package=THT]
  LED3 = LED - 5mm [color="Red (633nm)" package="5 mm [THT]"]
  LD1118 = V_REG_LD1117VXX [package=78xxl]
  R4 = Resistor [tolerance=±5% resistance=100 package=THT]
  LED4 = LED - 5mm [color="Red (633nm)" package="5 mm [THT]"]
  IN_5v = female pin header, 2 pins [form="♀ (female)"]

nets:
  N1: U1.RESET, S4.2, RESET.pin1, 10K.Pin_0
  N2: U1.D0_(RX), D0_(RX).pin1
  N3: U1.D1_(TX), D1_(TX).pin1
  N4: U1.D2, D2.pin1
  N5: U1.D3_(PWM), D3_(PWM).pin1
  N6: U1.D4, D4.pin1
  N7: U1.VCC, U1.AVCC, U1.AREF, 100nF.1, V1.V+, VIN.pin1, 10K.Pin_1
  N8: U1.GND#7, 100nF.0, V1.V-, S4.1, GND.pin1, GND.pin2
  N9: U1.XLAT1, XTAL1.pin_1, 18pF1.0
  N10: U1.XLAT2, XTAL1.pin_0, 18pF.0
  N11: U1.D5_(PWM), D5_(PWM).pin1
  N12: U1.D6_(PWM), D6_(PWM).pin1
  N13: U1.D7, D7.pin1
  N14: U1.D8, D8.pin1
  N15: U1.D9_(PWM), D9_(PWM).pin1
  N16: U1.D10_(PWM), D10_(PWM).pin1
  N17: U1.D11_(PWM), D11_(PWM).pin1
  N18: U1.D12, D12.pin1
  N19: U1.D13, 680Ω.Pin_1, D13.pin1
  N20: U1.GND#21, LED-PIN13.cathode, 18pF.1, 18pF1.1
  N21: U1.A0, A0.pin1
  N22: U1.A1, A1.pin1
  N23: U1.A2, A2.pin1
  N24: U1.A3, A3.pin1
  N25: U1.A4, A4/SDA.pin1
  N26: U1.A5, A5/SCL.pin1
  N27: 680Ω.Pin_0, LED-PIN13.anode
  GND: J1.GND, R1.Pin_0, IN_12v-.pin1, LM7805.GND, C2.-, IN_5v+1.pin1, LED3.cathode, LD1118.GND, LED4.cathode, IN_5v.pin1
  N28: J1.PWR, switch1.S, IN_12v+.pin1
  N29: ON_12v.cathode, R1.Pin_1
  N30: ON_12v.anode, LM7805.input_voltage
  N31: LM7805.output_voltage, C2.+
  N32: R3.Pin_0, LED3.anode
  N33: R3.Pin_1, LD1118.IN, IN_5v.pin2
  N34: LD1118.OUT, R4.Pin_1
  N35: R4.Pin_0, LED4.anode
