# Fritzing sketch v7 (saved by Fritzing 0.9.3b)
circuit board: 10cm x 6.5cm
breadboards: 1

parts:
  10K = Resistor [tolerance=±5% resistance=220 package=THT]
  +5V = Battery
  22p = Capacitor [package=cap-pth-small-kit]
  22p_2 = Capacitor [package=cap-pth-small-kit]
  part = Ceramic Capacitor [capacitance=100nF package="100 mil [THT, multilayer]"]
  LDR-A0 = Capacitor [package=cap-pth-small-kit]
  1 = atmega328 [package=dip]
  13 = LED - 3mm [color="Red (633nm)" package="3 mm [THT]"]
  1K = Resistor [tolerance=±5% resistance=220 package=THT]
  12 = LED - 3mm [color="Red (633nm)" package="3 mm [THT]"]
  1K_2 = Resistor [tolerance=±5% resistance=220 package=THT]
  11 = LED - 3mm [color="Red (633nm)" package="3 mm [THT]"]
  1K_3 = Resistor [tolerance=±5% resistance=220 package=THT]
  10 = LED - 3mm [color="Red (633nm)" package="3 mm [THT]"]
  1K_4 = Resistor [tolerance=±5% resistance=220 package=THT]
  9 = LED - 3mm [color="Red (633nm)" package="3 mm [THT]"]
  1K_5 = Resistor [tolerance=±5% resistance=220 package=THT]
  E_B_C = TRANSISTOR_NPN [package=to-92-ammo]
  - = Diode [package=diode-1n4001]
  10K_2 = Resistor [tolerance=±5% resistance=220 package=THT]
  LED = Capacitor [package=cap-pth-small-kit]
  part_2 = Arduino Uno (Rev3)
  part_3 = Capacitor [package=cap-pth-small-kit]
  100K = Resistor [tolerance=±5% resistance=220 package=THT]
  A0 = Capacitor [package=cap-pth-small-kit]
  L293D_DRIVER = L293D [package=THT]
  GND_M = Capacitor [package=cap-pth-small-kit]
  + = Capacitor [package=cap-pth-small-kit]
  ON = LED - 3mm [color="Red (633nm)" package="3 mm [THT]"]
  1K_6 = Resistor [tolerance=±5% resistance=220 package=THT]
  Reset = Momentary Switch [package=ksa_sealed_tac_switch]

nets:
  N1: 10K.Pin_0, part.1, 1.RESET, part_2.RESET, Reset.4
  VCC: +5V.-, 1.VCC, 1.AVCC, 1.AREF, -.C, part_2.5V, 100K.Pin_1, L293D_DRIVER.Enable_1, L293D_DRIVER.Enable_2, L293D_DRIVER.+V, +.1, 1K_6.Pin_1
  GND: +5V.+, 22p.1, 22p_2.1, LDR-A0.2, 1.GND, E_B_C.E, LED.2, part_2.GND, L293D_DRIVER.0V, GND_M.2, ON.cathode, Reset.2
  N2: 22p.2, 1.XLAT1
  N3: 22p_2.2, 1.XLAT2
  N4: LDR-A0.1, 100K.Pin_0, A0.1
  N5: 1.D0_(RX), part_2.D0/RX
  N6: 1.D1_(TX), part_2.D1/TX
  N7: 1.D2, part_2.D2
  N8: 1.D3_(PWM), part_2.D3_PWM
  N9: 1.D4, part_2.D4
  N10: 1.D5_(PWM), part_2.D5_PWM, L293D_DRIVER.In_2
  N11: 1.D6_(PWM), part_2.D6_PWM, L293D_DRIVER.In_1
  N12: 1.D7, part_2.D7
  N13: 1.D8, part_2.D8
  N14: 1.D9_(PWM), 1K_5.Pin_1, part_2.D9_PWM, L293D_DRIVER.In_3
  N15: 1.D10_(PWM), 1K_4.Pin_1, part_2.D10_PWM/SS, L293D_DRIVER.In_4
  N16: 1.D11_(PWM), 1K_3.Pin_1, part_2.D11_PWM/MOSI
  N17: 1.D12, 1K_2.Pin_1, part_2.D12/MISO, part_3.2
  N18: 1.D13, 1K.Pin_1, part_2.D13/SCK
  N19: 1.A0, part_2.A0, A0.2
  N20: 1.A1, part_2.A1
  N21: 1.A2, part_2.A2
  N22: 1.A3, part_2.A3
  N23: 1.A4, part_2.A4/SDA
  N24: 1.A5, part_2.A5/SCL
  N25: 13.cathode, 12.cathode, 11.cathode, 10.cathode, 9.cathode, LED.1
  N26: 13.anode, 1K.Pin_0
  N27: 12.anode, 1K_2.Pin_0
  N28: 11.anode, 1K_3.Pin_0
  N29: 10.anode, 1K_4.Pin_0
  N30: 9.anode, 1K_5.Pin_0
  N31: E_B_C.B, 10K_2.Pin_0
  N32: E_B_C.C, -.A
  N33: 10K_2.Pin_1, part_3.1
  N34: L293D_DRIVER.+Vmotor, GND_M.1
  N35: ON.anode, 1K_6.Pin_0

notes:
  GND
  16Mhz
  A5  A4  A3  A2  A1  A0
  13 12 11´10´ 9´
  RST 0  1  2  3´ 4
  3,3V
  +5V - TX RX
  ATMEGA 328P-PU
  Bluetooth
  5V GND TX RX
  4
  7
  8
  RX TX
  -  +  s
  Servo
  XL
  E
  T
  -
  2
  3
  SR04
  NC    C     NO
  0,1uf
  Relay D12
  RST
  CH_DP
  TX
  3V3
  RX
  IO0
  IO2
  0
  SCL
  SDA
  ESP8266 / IN
  I2C-LCD 16x2
  Relay
  -  +
  +  +  -
  x1 x2 D5´D6´D7 D8
  A0 A1 A2 A3 A4 A5
  7  6´ 5´ 4  3´ 2  1  0
  GND 13 12 11´10´9´ 8
  5V
  USB-Serial
  www.arduprofe.com
  BOARD MODEL
  -------------------------------------------
  OPEN  SOURCE ELECTRONICS
  PROT TYPING PLATFORM
  UNO  R3 - EXTENDED
  EXTENDED
  GND +V TX RX DT
  TX   RX
  RX  TX
  +5V
  monteverdeltda.com
  Dev. FelipheGomez
  UNO EXTENDED MKR 8000
  GARDEN-PRO
  MOTOR
  10
  9
  6
  5
  ::out ::
  +V.M
  --->
  EN I6 O6  GND  O5 I5 +Vs
  +V I10 O10 GND  O9 I9 EN
  L293D
  328P-PU
  open source
  2222A
  1N400x
  hardware
  +
  _
  10uf
  1838B
  S
  DANGER
  Electric Shock Risk
  PELIGRO
  Riesgo Eléctrico
  Vcc
  WWW.ARDUINO.CC - MADE IN ITALY
  CLK
  CS
  DIN
  VCC
  8x8>>
  N0  C  NC
  IR
  -------------------------------------------------------------------
  HC-06
  ------------
  ---
  --
