# Fritzing sketch 12v to 5v (saved by Fritzing 0.9.3b)
circuit board: 3.09898cm x 3.10353cm
breadboards: 1

parts:
  U1 = Voltage Regulator - 5V [package="TO220 [THT]"]
  Power_plug1 = Power plug
  S1 = Toggle Switch [package=THT]
  C1 = Electrolytic Capacitor [capacitance=1µF package="100 mil [THT, electrolytic]"]
  J3 = female pin header, 2 pins [form="♀ (female)"]
  C2 = Electrolytic Capacitor [capacitance=1µF package="100 mil [THT, electrolytic]"]

nets:
  N1: U1.input_voltage, S1.COM, C1.+
  GND: U1.GND, Power_plug1.GND, C1.-, J3.pin2, C2.-
  N2: U1.output_voltage, J3.pin1, C2.+
  N3: Power_plug1.VCC, S1.L2

notes:
  Este ejemplo utiliza un regulador de voltaje 7805 para regular el voltaje a 5 voltios. Hay un interruptor para encender y apagar el circuito. La batería debe ser de al menos 7V DC.
