# Fritzing sketch DUAL VOLTAGE REG V1 (saved by Fritzing 0.9.3b)
circuit board: 8.46667cm x 5.64444cm
breadboards: 1

parts:
  U1 = Voltage Regulator - 12V [package=NTE966]
  U2 = Voltage Regulator - 8V [package=NTE964]
  J1 = Screw terminal - 2 pins [package=THT]
  J2 = Screw terminal - 2 pins [package=THT]
  J3 = Screw terminal - 2 pins [package=THT]
  C1 = Electrolytic Capacitor [capacitance=2.2mF voltage=35V package="300 mil [THT, electrolytic]"]
  C2 = Electrolytic Capacitor [capacitance=1mF voltage=20V package="200 mil [THT, electrolytic]"]
  C3 = Electrolytic Capacitor [capacitance=3.3mF voltage=16V package="200 mil [THT, electrolytic]"]
  LED1 = LED - 5mm [color="Green (565nm)" package="5 mm [THT]"]
  LED2 = LED - 5mm [color="Blue (505nm)" package="5 mm [THT]"]
  R1 = Resistor [tolerance=±5% resistance=330 package=THT]
  R2 = Resistor [tolerance=±5% resistance=330 package=THT]

nets:
  N1: U1.input_voltage, U1.output_voltage, U2.input_voltage, U2.output_voltage, J1.pin2, J2.pin2, J3.pin2, C1.+, C2.+, C3.+, LED1.cathode, LED2.cathode
  GND: U1.GND, U2.GND, J1.pin1, J2.pin1, J3.pin1, C1.-, C2.-, C3.-, R1.Pin_1, R2.Pin_1
  N2: LED1.anode, R1.Pin_0
  N3: LED2.anode, R2.Pin_0

custom parts:
  Voltage Regulator - 12V: 12V DC Voltage Regulator
  Voltage Regulator - 8V: 8V DC Voltage Regulator
