# Fritzing sketch v1 (saved by Fritzing 0.9.3b)
breadboards: 1

parts:
  Power_In = Power plug
  S1 = Toggle Switch [package=THT]
  5v- = female pin header, 5 pins [form="♀ (female)"]
  5v+ = female pin header, 5 pins [form="♀ (female)"]
  C4 = Electrolytic Capacitor [capacitance=100μF package="100 mil [THT, electrolytic]"]
  U4 = Voltage Regulator - 5V [package="TO220 [THT]"]

nets:
  GND: Power_In.GND, 5v-.pin1, 5v-.pin2, 5v-.pin3, 5v-.pin4, 5v-.pin5, C4.-, U4.GND
  N1: Power_In.VCC, S1.L1
  N2: S1.COM, U4.input_voltage
  N3: 5v+.pin1, 5v+.pin2, 5v+.pin3, 5v+.pin4, 5v+.pin5, C4.+, U4.output_voltage
