# Fritzing sketch 002 (saved by Fritzing 0.9.3b)
breadboards: 3

parts:
  IC2 = MICROCONTROLLER [package=dil28-3]
  XTAL2 = Crystal [frequency="16 Mhz" package=THT]
  C6 = Ceramic Capacitor [capacitance=22pF package="100 mil [THT, multilayer]"]
  C7 = Ceramic Capacitor [capacitance=22pF package="100 mil [THT, multilayer]"]
  Power_plug4 = Power plug
  U2 = Voltage Regulator - 5V [package="TO220 [THT]"]
  C8 = Electrolytic Capacitor [capacitance=100µF package="100 mil [THT, electrolytic]"]
  C9 = Electrolytic Capacitor [capacitance=100µF package="100 mil [THT, electrolytic]"]
  R3 = Resistor [tolerance=±5% resistance=1k package=THT]
  LED2 = LED - 5mm [color="Red (633nm)" package="5 mm [THT]"]
  R4 = Resistor [tolerance=±5% resistance=10k package=THT]
  S4 = Pushbutton [package="[THT]"]
  J5 = female pin header, 8 pins [form="♀ (female)"]
  J6 = female pin header, 4 pins [form="♀ (female)"]
  J7 = female pin header, 14 pins [form="♀ (female)"]
  C10 = Ceramic Capacitor [capacitance=100nF package="100 mil [THT, multilayer]"]
  J8 = female pin header, 6 pins [form="♀ (female)"]
  U3 = SWITCH_SPDT [package=kps-1290]
  Power_plug5 = Power plug
  Power_plug6 = Power plug
  C11 = Electrolytic Capacitor [capacitance=100µF package="100 mil [THT, electrolytic]"]
  U4 = Voltage Regulator - 5V [package="TO220 [THT]"]
  C12 = Electrolytic Capacitor [capacitance=100µF package="100 mil [THT, electrolytic]"]
  R5 = Resistor [tolerance=±5% resistance=1k package=THT]
  S5 = Pushbutton [package="[THT]"]
  LED3 = LED - 5mm [color="Red (633nm)" package="5 mm [THT]"]
  U5 = atmega168 [package=dip]  # not connected

nets:
  N1: IC2.PC6(_RESET), R4.Pin_1, S4.Pin_1, S4.Pin_2, J5.pin1, C10.1
  N2: IC2.PD0(RXD), J5.pin2, J8.pin3
  N3: IC2.PD1(TXD), J5.pin3, J8.pin2
  N4: IC2.PD2(INT0), J5.pin4
  N5: IC2.PD3(INT1), J5.pin5
  N6: IC2.PD4(XCK_T0), J5.pin6
  N7: IC2.VCC, IC2.AVCC, U2.output_voltage, C9.+, R3.Pin_0, R4.Pin_0, J5.pin7, J7.pin6
  GND: IC2.GND, IC2.AGND, C6.1, C7.0, Power_plug4.GND, U2.GND, C8.-, C9.-, LED2.cathode, S4.Pin_3, S4.Pin_4, J5.pin8, J7.pin8, J8.pin6, Power_plug5.GND
  N8: IC2.PB6(XTAL1_TOSC1), XTAL2.pin_0, C6.0
  N9: IC2.PB7(XTAL2_TOSC2), XTAL2.pin_1, C7.1
  N10: IC2.PD5(T1), J6.pin1
  N11: IC2.PD6(AIN0), J6.pin2
  N12: IC2.PD7(AIN1), J6.pin3
  N13: IC2.PB0(ICP), J6.pin4
  N14: IC2.PB1(OC1A), J7.pin1
  N15: IC2.PB2(SS_OC1B), J7.pin2
  N16: IC2.PB3(MOSI_OC2), J7.pin3
  N17: IC2.PB4(MISO), J7.pin4
  N18: IC2.PB5(SCK), J7.pin5
  N19: IC2.AREF, J7.pin7
  N20: IC2.PC0(ADC0), J7.pin9
  N21: IC2.PC1(ADC1), J7.pin10
  N22: IC2.PC2(ADC2), J7.pin11
  N23: IC2.PC3(ADC3), J7.pin12
  N24: IC2.PC4(ADC4_SDA), J7.pin13
  N25: IC2.PC5(ADC5_SCL), J7.pin14
  VCC: Power_plug4.VCC, U2.input_voltage, C8.+, Power_plug5.VCC
  N26: R3.Pin_1, LED2.anode
  N27: C10.0, J8.pin1
  N28: U3.P, C11.+, U4.input_voltage
  N29: U3.S, Power_plug6.VCC
  GND_2: Power_plug6.GND, C11.-, U4.GND, C12.-, S5.Pin_3, S5.Pin_4, LED3.cathode
  N30: U4.output_voltage, C12.+, R5.Pin_0
  N31: R5.Pin_1, LED3.anode
  N32: S5.Pin_1, S5.Pin_2
