# Fritzing sketch 003 (saved by Fritzing 0.9.3b)
breadboards: 3

parts:
  IC2 = MICROCONTROLLER [package=dil28-3]
  XTAL2 = Crystal [frequency="16 Mhz" package=THT]
  C6 = Ceramic Capacitor [capacitance=22pF package="100 mil [THT, multilayer]"]
  C7 = Ceramic Capacitor [capacitance=22pF package="100 mil [THT, multilayer]"]
  Power_plug4 = Power plug
  U2 = Voltage Regulator - 5V [package="TO220 [THT]"]
  C8 = Electrolytic Capacitor [capacitance=100µF package="100 mil [THT, electrolytic]"]
  C9 = Electrolytic Capacitor [capacitance=100µF package="100 mil [THT, electrolytic]"]
  R3 = Resistor [tolerance=±5% resistance=1k package=THT]
  LED2 = LED - 5mm [color="Red (633nm)" package="5 mm [THT]"]
  R4 = Resistor [tolerance=±5% resistance=10k package=THT]
  S4 = Pushbutton [package="[THT]"]
  J5 = female pin header, 8 pins [form="♀ (female)"]
  J6 = female pin header, 4 pins [form="♀ (female)"]
  J7 = female pin header, 14 pins [form="♀ (female)"]
  C10 = Ceramic Capacitor [capacitance=100nF package="100 mil [THT, multilayer]"]
  J8 = female pin header, 6 pins [form="♀ (female)"]
  Power_plug5 = Power plug
  Power_plug6 = Power plug
  U4 = Voltage Regulator - 5V [package="TO220 [THT]"]
  C12 = Electrolytic Capacitor [capacitance=100µF package="100 mil [THT, electrolytic]"]
  LED3 = LED - 5mm [color="Red (633nm)" package="5 mm [THT]"]
  U5 = V_REG_LD1117VXX [package=78xxl]
  LED5 = LED - 5mm [color="Red (633nm)" package="5 mm [THT]"]
  R7 = Resistor [tolerance=±5% resistance=100 package=THT]
  J9 = female pin header, 8 pins [form="♀ (female)"]
  J11 = female pin header, 8 pins [form="♀ (female)"]
  J12 = female pin header, 8 pins [form="♀ (female)"]
  J13 = female pin header, 8 pins [form="♀ (female)"]
  R8 = Resistor [tolerance=±5% resistance=100 package=THT]  # not connected
  J14 = female pin header, 8 pins [form="♀ (female)"]
  J15 = female pin header, 8 pins [form="♀ (female)"]
  R9 = Resistor [tolerance=±5% resistance=270 package=THT]
  LED6 = LED - 5mm [color="Red (633nm)" package="5 mm [THT]"]
  R10 = Resistor [tolerance=±5% resistance=1k package=THT]
  U3 = SWITCH_SPDT [package=kps-1290]

nets:
  N1: IC2.PC6(_RESET), R4.Pin_1, S4.Pin_1, S4.Pin_2, J5.pin1, C10.1
  N2: IC2.PD0(RXD), J5.pin2, J8.pin3
  N3: IC2.PD1(TXD), J5.pin3, J8.pin2
  N4: IC2.PD2(INT0), J5.pin4
  N5: IC2.PD3(INT1), J5.pin5
  N6: IC2.PD4(XCK_T0), J5.pin6
  N7: IC2.VCC, IC2.AVCC, U2.output_voltage, C9.+, R3.Pin_0, R4.Pin_0, J5.pin7, J7.pin6
  GND: IC2.GND, IC2.AGND, C6.1, C7.0, Power_plug4.GND, U2.GND, C8.-, C9.-, LED2.cathode, S4.Pin_3, S4.Pin_4, J5.pin8, J7.pin8, J8.pin6, Power_plug5.GND
  N8: IC2.PB6(XTAL1_TOSC1), XTAL2.pin_0, C6.0
  N9: IC2.PB7(XTAL2_TOSC2), XTAL2.pin_1, C7.1
  N10: IC2.PD5(T1), J6.pin1
  N11: IC2.PD6(AIN0), J6.pin2
  N12: IC2.PD7(AIN1), J6.pin3
  N13: IC2.PB0(ICP), J6.pin4
  N14: IC2.PB1(OC1A), J7.pin1
  N15: IC2.PB2(SS_OC1B), J7.pin2
  N16: IC2.PB3(MOSI_OC2), J7.pin3
  N17: IC2.PB4(MISO), J7.pin4
  N18: IC2.PB5(SCK), J7.pin5
  N19: IC2.AREF, J7.pin7
  N20: IC2.PC0(ADC0), J7.pin9
  N21: IC2.PC1(ADC1), J7.pin10
  N22: IC2.PC2(ADC2), J7.pin11
  N23: IC2.PC3(ADC3), J7.pin12
  N24: IC2.PC4(ADC4_SDA), J7.pin13
  N25: IC2.PC5(ADC5_SCL), J7.pin14
  VCC: Power_plug4.VCC, U2.input_voltage, C8.+, Power_plug5.VCC
  N26: R3.Pin_1, LED2.anode
  N27: C10.0, J8.pin1
  GND_2: Power_plug6.GND, U4.GND, C12.-, LED3.cathode, U5.GND, LED5.cathode, J9.pin1, J9.pin2, J9.pin3, J9.pin4, J9.pin5, J9.pin6, J9.pin7, J9.pin8, J12.pin1, J12.pin2, J12.pin3, J12.pin4, J12.pin5, J12.pin6, J12.pin7, J12.pin8, J14.pin1, J14.pin2, J14.pin3, J14.pin4, J14.pin5, J14.pin6, J14.pin7, J14.pin8, R10.Pin_1
  N28: Power_plug6.VCC, U3.S
  N29: U4.input_voltage, J11.pin1, J11.pin2, J11.pin3, J11.pin4, J11.pin5, J11.pin6, J11.pin7, J11.pin8, LED6.anode, U3.P
  N30: U4.output_voltage, C12.+, U5.IN, J13.pin1, J13.pin2, J13.pin3, J13.pin4, J13.pin5, J13.pin6, J13.pin7, J13.pin8, R9.Pin_1
  N31: LED3.anode, R9.Pin_0
  N32: U5.OUT, R7.Pin_1, J15.pin1, J15.pin2, J15.pin3, J15.pin4, J15.pin5, J15.pin6, J15.pin7, J15.pin8
  N33: LED5.anode, R7.Pin_0
  N34: LED6.cathode, R10.Pin_0

notes:
  Regulador 5v y 3.3v
