# Fritzing sketch Fuente de alimentación de 12V-3A - out 5v and 3.v (saved by Fritzing 0.9.3b)
breadboards: 2

parts:
  Power_plug6 = Power plug
  C11 = Electrolytic Capacitor [capacitance=100µF voltage=35V package="100 mil [THT, electrolytic]"]
  U4 = Voltage Regulator - 5V [package="TO220 [THT]"]
  C12 = Electrolytic Capacitor [capacitance=100µF package="100 mil [THT, electrolytic]"]
  R5 = Resistor [tolerance=±5% resistance=270 package=THT]
  LED3 = LED - 5mm [color="Red (633nm)" package="5 mm [THT]"]
  LED4 = LED - 5mm [color="Red (633nm)" package="5 mm [THT]"]
  R6 = Resistor [tolerance=±5% resistance=1k package=THT]
  U5 = V_REG_LD1117VXX [package=78xxl]
  LED5 = LED - 5mm [color="Red (633nm)" package="5 mm [THT]"]
  R7 = Resistor [tolerance=±5% resistance=100 package=THT]
  J9 = female pin header, 8 pins [form="♀ (female)"]
  J11 = female pin header, 8 pins [form="♀ (female)"]
  J12 = female pin header, 8 pins [form="♀ (female)"]
  J13 = female pin header, 8 pins [form="♀ (female)"]
  U3 = SPST Switch [package=switch-spdt]

nets:
  GND: Power_plug6.GND, C11.-, U4.GND, C12.-, LED3.cathode, R6.Pin_1, U5.GND, LED5.cathode, J9.pin1, J9.pin2, J9.pin3, J9.pin4, J9.pin5, J9.pin6, J9.pin7, J9.pin8, J12.pin1, J12.pin2, J12.pin3, J12.pin4, J12.pin5, J12.pin6, J12.pin7, J12.pin8
  N1: Power_plug6.VCC, U3.S
  N2: C11.+, U4.input_voltage, LED4.anode, J11.pin1, J11.pin2, J11.pin3, J11.pin4, J11.pin5, J11.pin6, J11.pin7, J11.pin8, U3.P
  N3: U4.output_voltage, C12.+, R5.Pin_1, U5.IN, J13.pin1, J13.pin2, J13.pin3, J13.pin4, J13.pin5, J13.pin6, J13.pin7, J13.pin8
  N4: R5.Pin_0, LED3.anode
  N5: LED4.cathode, R6.Pin_0
  N6: U5.OUT, R7.Pin_1
  N7: LED5.anode, R7.Pin_0

notes:
  Regulador 5v y 3.3v
