# Fritzing sketch 001 (saved by Fritzing 0.9.3b)
breadboards: 1

parts:
  LED1 = LED - 5mm [color="Red (633nm)" package="5 mm [THT]"]
  R1 = Resistor [tolerance=±5% resistance=220 package=THT]
  C2 = Electrolytic Capacitor [capacitance=10μF package="0605 [SMD, electrolytic]"]
  LED2 = LED - 5mm [color="Red (633nm)" package="5 mm [THT]"]
  R2 = Resistor [tolerance=±5% resistance=220 package=THT]
  C3 = Ceramic Capacitor [capacitance=100nF package="100 mil [THT, multilayer]"]
  C4 = Ceramic Capacitor [capacitance=100nF package="100 mil [THT, multilayer]"]
  XTAL1 = Crystal [frequency="16 Mhz" package=THT]
  Part1 = FTDI Basic Programmer
  U2 = atmega328 [package=dip]
  S1 = Pushbutton [package="[THT]"]
  U1 = Voltage Regulator - 5V [package="TO220 [THT]"]
  C1 = Electrolytic Capacitor [capacitance=10μF package="200 mil [THT, electrolytic]"]
  PW_IN = Power plug
  PW_OUT = Power plug
  VALVE1 = Plastic Solenoid Valve  # not connected
  LED_ALERT = female pin header, 2 pins [form="♀ (female)"]
  BUZZ_ALERT = female pin header, 2 pins [form="♀ (female)"]
  R3 = Resistor [tolerance=±5% resistance=220 package=THT]
  R4 = Resistor [tolerance=±5% resistance=100 package=THT]
  DATA_OUT = female pin header, 3 pins [form="♀ (female)"]
  DATA_OUT2 = female pin header, 3 pins [form="♀ (female)"]
  Battery = female pin header, 2 pins [form="♀ (female)"]
  LED3 = LED - 5mm [color="Red (633nm)" package="5 mm [THT]"]  # not connected
  Water_Level_Sensor1 = Water Level Sensor
  BAT1 = BC9VPC [package=bc9vpc]  # not connected
  VCC1 = Battery block 9V

nets:
  N1: LED1.cathode, R1.Pin_1
  VCC: LED1.anode, C2.+, Part1.POWER, U2.VCC, U2.AVCC, U1.output_voltage, DATA_OUT.pin2, Water_Level_Sensor1.VCC
  GND: R1.Pin_0, C2.-, R2.Pin_1, C3.0, C4.1, Part1.GND, U2.RESET, U2.GND, S1.Pin_1, S1.Pin_2, S1.Pin_3, S1.Pin_4, U1.GND, C1.-, PW_IN.GND, PW_OUT.GND, BUZZ_ALERT.pin1, R3.Pin_1, Battery.pin2, VCC1.-
  N2: LED2.cathode, R2.Pin_0
  N3: LED2.anode, U2.D13
  N4: C3.1, XTAL1.pin_1, U2.XLAT1
  N5: C4.0, XTAL1.pin_0, U2.XLAT2
  N6: Part1.RXI, U2.D1_(TX)
  N7: Part1.TXO, U2.D0_(RX)
  N8: U2.D3_(PWM), R4.Pin_0
  N9: U2.A0, DATA_OUT.pin3, DATA_OUT2.pin3, Water_Level_Sensor1.SIG
  VCC_2: U1.input_voltage, C1.+, PW_IN.VCC, PW_OUT.VCC, Battery.pin1, VCC1.+
  N10: LED_ALERT.pin1, R3.Pin_0
  N11: BUZZ_ALERT.pin2, R4.Pin_1
  N12: DATA_OUT.pin1, DATA_OUT2.pin1, Water_Level_Sensor1.GND

custom parts:
  Water Level Sensor: A water level sensor. This sensor operates at 3V to 5V. The Sig (signal) pin outputs an analogue signal that is in proportion to the amount of water in contact with the sensor.

// code stored in the sketch: 001.ino
int red=2;
int green=3;
int blue=4;

void setup () {
  pinMode (red,OUTPUT);
  pinMode (green,OUTPUT);
  pinMode (blue,OUTPUT);
  Serial.begin (9600);
}
 
void loop() {
  // read the input on analog pin 0:
  int value = analogRead(A0)
  if (value > 500) {
    Serial.println("Very heavy Rain");
    digitalWrite (red,HIGH);
    digitalWrite(green,LOW);
    digitalWrite(blue,LOW);}
  else if ((value > 300) && (value <= 500)) {
    Serial.println("AVERAGE Rain");
    digitalWrite (green,HIGH);
    digitalWrite (red,LOW);
  } else {
    Serial.println("Dry Weather");
    digitalWrite (blue,HIGH);
    digitalWrite (red,LOW);
    digitalWrite (green,LOW);
	delay(100);
  }
}
