# Fritzing sketch 002 (saved by Fritzing 0.9.3b)

parts:
  Power_plug = Power plug
  LM7805 = Voltage Regulator - 5V [package="TO220 [THT]"]
  C1 = Electrolytic Capacitor [capacitance=100µF package="100 mil [THT, electrolytic]"]
  LED2 = LED - 5mm [color="Red (633nm)" package="5 mm [THT]"]
  LD1117 = V_REG_LD1117VXX [package=78xxl]
  LED3 = LED - 5mm [color="Red (633nm)" package="5 mm [THT]"]
  R3 = Resistor [tolerance=±5% resistance=100 package=THT]
  GND1 = female pin header, 8 pins [form="♀ (female)"]
  12v+ = female pin header, 8 pins [form="♀ (female)"]
  5v- = female pin header, 8 pins [form="♀ (female)"]
  5v+ = female pin header, 8 pins [form="♀ (female)"]
  GND3 = female pin header, 8 pins [form="♀ (female)"]
  3_3v+ = female pin header, 8 pins [form="♀ (female)"]
  R2 = Resistor [tolerance=±5% resistance=270 package=THT]
  LED1 = LED - 5mm [color="Red (633nm)" package="5 mm [THT]"]
  R1 = Resistor [tolerance=±5% resistance=1k package=THT]
  switch = SPST Switch [package=switch-spdt_lock.007s]
  S1 = Pushbutton [package="[THT]"]  # not connected
  J1 = female pin header, 14 pins [form="♀ (female)"]  # not connected
  U3 = atmega328 [package=dip]  # not connected
  J2 = female pin header, 14 pins [form="♀ (female)"]
  XTAL1 = Crystal [frequency="16 Mhz" package=THT]
  22pF-1 = Ceramic Capacitor [capacitance=22pF package="100 mil [THT, multilayer]"]  # not connected
  0_1µF = Ceramic Capacitor [capacitance=0.1µF package="100 mil [THT, multilayer]"]  # not connected
  22pF-2 = Ceramic Capacitor [capacitance=22pF package="100 mil [THT, multilayer]"]  # not connected

nets:
  GND: Power_plug.GND, LM7805.GND, C1.-, LED2.cathode, LD1117.GND, GND1.pin1, GND1.pin2, GND1.pin3, GND1.pin4, GND1.pin5, GND1.pin6, GND1.pin7, GND1.pin8, 5v-.pin1, 5v-.pin2, 5v-.pin3, 5v-.pin4, 5v-.pin5, 5v-.pin6, 5v-.pin7, 5v-.pin8, GND3.pin1, GND3.pin2, GND3.pin3, GND3.pin4, GND3.pin5, GND3.pin6, GND3.pin7, GND3.pin8, R1.Pin_1
  N1: Power_plug.VCC, switch.S
  N2: LM7805.input_voltage, 12v+.pin1, 12v+.pin2, 12v+.pin3, 12v+.pin4, 12v+.pin5, 12v+.pin6, 12v+.pin7, 12v+.pin8, LED1.anode, switch.P
  N3: LM7805.output_voltage, C1.+, LD1117.IN, 5v+.pin1, 5v+.pin2, 5v+.pin3, 5v+.pin4, 5v+.pin5, 5v+.pin6, 5v+.pin7, 5v+.pin8, R2.Pin_1
  N4: LED2.anode, R2.Pin_0
  N5: LD1117.OUT, R3.Pin_1, 3_3v+.pin1, 3_3v+.pin2, 3_3v+.pin3, 3_3v+.pin4, 3_3v+.pin5, 3_3v+.pin6, 3_3v+.pin7, 3_3v+.pin8
  N6: LED3.anode, R3.Pin_0
  N7: LED1.cathode, R1.Pin_0
  N8: J2.pin9, XTAL1.pin_0
  N9: J2.pin10, XTAL1.pin_1

notes:
  Regulador 12v - 5v y 3.3v
