# Fritzing sketch Alim labo (saved by Fritzing 0.7.11b)
breadboards: 5

parts:
  U1 = B250D Bridge Rectifier [package=THT]
  T1 = Transformer [part_number="2x12V 400mA" package="Through Hole"]
  T2 = Transformer [part_number="1x30V 4A" package="Through Hole"]
  U2 = B250D Bridge Rectifier [package=THT]
  Power_plug1 = Power plug
  IC1 = PICAXE-14M [part_number="IC1 - LM723" package=THT]  # not connected
  C10 = Electrolytic Capacitor [capacitance=4.7mF voltage=63V part_number=C10 package="300 mil [THT, electrolytic]"]
  C1 = Electrolytic Capacitor [capacitance=1mF voltage=25V part_number=C2 package="200 mil [THT, electrolytic]"]
  C1_2 = Electrolytic Capacitor [capacitance=1mF voltage=50V part_number=C1 package="200 mil [THT, electrolytic]"]
  R1 = Resistor [tolerance=±5% resistance=4.7k part_number=R1 power=999 package=THT]
  C3 = Electrolytic Capacitor [capacitance=100µF voltage=10V part_number=C3 package="100 mil [THT, electrolytic]"]
  D1 = Rectifier Diode [part_number=1N4001 package="300 mil [THT]"]
  R2 = Resistor [tolerance=±5% resistance=22 part_number=R2 power=999 package=THT]
  C4 = Ceramic Capacitor [capacitance=0.1nF part_number=C4 package="100 mil [THT, multilayer]"]
  R3 = Resistor [tolerance=±5% resistance=4.7k part_number=R3 power=999 package=THT]
  R9 = Resistor [tolerance=±5% resistance=2.2k part_number=R9 power=999 package=THT]
  C5 = Electrolytic Capacitor [capacitance=10µF voltage=25V part_number=C5 package="100 mil [THT, electrolytic]"]
  IC2 = DIP - 8 pins [part_number=LM741 package="DIP (Dual Inline) [THT]"]
  R4 = Resistor [tolerance=±5% resistance=0 part_number=R4 power=999 package=THT]
  R5 = Resistor [tolerance=±5% resistance=10k power=999 package=THT]  # not connected
  R6 = Resistor [tolerance=±5% resistance=4.7k part_number=R6 power=999 package=THT]
  C6 = Ceramic Capacitor [capacitance=1nF part_number=C6 package="100 mil [THT, multilayer]"]
  R7 = Resistor [tolerance=±5% resistance=1k power=999 package=THT]
  P1 = Trimmer Potentiometer [maximum_resistance=50kΩ part_number=P1 package=THT]
  -Us = female pin header, 1 pin [form="♀ (female)" part_number=-Us]
  -U = female pin header, 1 pin [form="♀ (female)" part_number=-U]
  J1 = female pin header, 1 pin [form="♀ (female)"]
  +Us = female pin header, 1 pin [form="♀ (female)" part_number=+Us]
  +U = female pin header, 1 pin [form="♀ (female)" part_number=+U]
  R24 = Resistor [tolerance=±5% resistance=47 part_number=R24 power=999 package=THT]  # not connected
  C12 = Ceramic Capacitor [capacitance=100nF part_number=C12 package="100 mil [THT, multilayer]"]  # not connected
  R22 = Resistor [tolerance=±5% resistance=4.7k power=1W part_number=R22 package=THT]
  D2 = Rectifier Diode [part_number=1N4148 package="300 mil [THT]"]
  D3 = Rectifier Diode [part_number=1N4148 package="300 mil [THT]"]
  R8 = Resistor [tolerance=±5% resistance=4.7k power=999 part_number=R8 package=THT]
  C7 = Ceramic Capacitor [capacitance=0.1nF part_number=C7 package="100 mil [THT, multilayer]"]
  D4 = Rectifier Diode [part_number=1N4148 package="300 mil [THT]"]  # not connected
  C9 = Electrolytic Capacitor [capacitance=47µF voltage=63V part_number=C9 package="100 mil [THT, electrolytic]"]
  R15 = Resistor [tolerance=±5% resistance=15k power=999 package=THT]
  R16 = Resistor [tolerance=±5% resistance=0 power=999 package=THT]
  R14 = Resistor [tolerance=±5% resistance=4.7k power=999 package=THT]
  IC3 = DIP - 8 pins [part_number=LM741 package="DIP (Dual Inline) [THT]"]
  P2 = Trimmer Potentiometer [maximum_resistance=10kΩ package=THT]
  R13 = Resistor [tolerance=±5% resistance=4.7k power=999 package=THT]
  C8 = Ceramic Capacitor [capacitance=56pF package="100 mil [THT, multilayer]"]
  D5 = Rectifier Diode [part_number=1N4001 package="300 mil [THT]"]  # not connected
  R12 = Resistor [tolerance=±5% resistance=4.7k power=999 package=THT]
  D6 = Zener Diode [part_number=1N4732A breakdown_voltage=3.3V package="300 mil [THT]"]
  R10 = Resistor [tolerance=±5% resistance=1k power=999 package=THT]
  R11 = Resistor [tolerance=±5% resistance=470 power=1W package=THT]
  D7 = LED - 5mm [color="Red (635nm)" current=3A package="5 mm [THT]"]
  T1_2 = PNP-Transistor [part_number=BC559C package="TO92 [THT]"]
  R17 = Resistor [tolerance=±5% resistance=10 package=THT]
  R18 = Resistor [tolerance=±5% resistance=0.2 package=THT]
  R19 = Resistor [tolerance=±5% resistance=0.2 package=THT]
  T2_2 = NPN-Transistor [part_number=BD241 package="TO92 [THT]"]
  T3 = npn-Powertransistor [part_number=2N3055 package="TO220 [THT]"]
  T4 = npn-Powertransistor [part_number=2N3055 package="TO220 [THT]"]
  T5 = npn-Powertransistor [part_number=2N3055 package="TO220 [THT]"]
  T6 = npn-Powertransistor [part_number=2N3055 package="TO220 [THT]"]
  T7 = npn-Powertransistor [part_number=2N3055 package="TO220 [THT]"]
  R20 = Resistor [tolerance=±5% resistance=0.2 package=THT]
  R27 = Resistor [tolerance=±5% resistance=0.2 package=THT]
  R28 = Resistor [tolerance=±5% resistance=0.2 package=THT]
  D8 = Rectifier Diode [part_number=1N4001 package="300 mil [THT]"]
  R21 = Resistor [tolerance=±5% resistance=0.2 power=3W package=THT]
  R23 = Resistor [tolerance=±5% resistance=47 power=999 package=THT]
  C11 = Ceramic Capacitor [capacitance=820nF package="100 mil [THT, multilayer]"]

nets:
  N1: U1.Pin_1, C1_2.+, D1.cathode, IC2.pin7, IC3.pin7, R10.Pin_0, T1_2.E
  N2: U1.Pin_2, C1.-, IC2.pin4, IC3.pin4
  N3: U1.Pin_3, T1.4
  N4: U1.Pin_4, T1.6
  N5: T1.2, T2.2, Power_plug1.VCC
  N6: T1.3, T2.3, Power_plug1.GND
  N7: T1.5, C1.+, C1_2.-, C3.-, C5.-, J1.pin1, +Us.pin1, R8.Pin_1, P2.leg2, D7.cathode, R23.Pin_1, C11.1
  N8: T2.4, U2.Pin_3
  N9: T2.5, U2.Pin_4
  N10: U2.Pin_1, C10.+, T2_2.E, T3.emitter, T4.emitter, T5.emitter, T6.emitter, T7.emitter, D8.cathode
  N11: U2.Pin_2, C10.-, -U.pin1, R22.Pin_0, C9.-
  N12: R1.Pin_1, C3.+
  N13: D1.anode, R2.Pin_0, R3.Pin_1, R9.Pin_0, C5.+, R4.Pin_0, R15.Pin_0, R16.Pin_0
  N14: C4.0, R3.Pin_0
  N15: R9.Pin_1, T2_2.B
  N16: IC2.pin2, D2.cathode, D3.anode, R8.Pin_0, C7.0
  N17: IC2.pin3, R6.Pin_1, C6.0, D2.anode, D3.cathode
  N18: IC2.pin6, C7.1
  N19: R4.Pin_1, P1.leg1, P1.wiper
  N20: C6.1, R7.Pin_0
  N21: R7.Pin_1, P1.leg2, -Us.pin1
  N22: +U.pin1, C9.+, R21.Pin_0, R23.Pin_0, C11.0
  N23: R22.Pin_1, R14.Pin_1, R17.Pin_1, R18.Pin_1, R19.Pin_1, R20.Pin_1, R27.Pin_1, R28.Pin_1, D8.anode, R21.Pin_1
  N24: R15.Pin_1, R16.Pin_1, P2.leg1
  N25: R14.Pin_0, IC3.pin2, C8.1
  N26: IC3.pin3, R13.Pin_1
  N27: IC3.pin6, C8.0, R12.Pin_1
  N28: P2.wiper, R13.Pin_0
  N29: R12.Pin_0, D6.anode
  N30: D6.cathode, R10.Pin_1, T1_2.B
  N31: R11.Pin_0, T1_2.C
  N32: R11.Pin_1, D7.anode
  N33: R17.Pin_0, T2_2.C, T3.base, T4.base, T5.base, T6.base, T7.base
  N34: R18.Pin_0, T3.collector
  N35: R19.Pin_0, T4.collector
  N36: T5.collector, R20.Pin_0
  N37: T6.collector, R27.Pin_0
  N38: T7.collector, R28.Pin_0

custom parts:
  B250D Bridge Rectifier: Converts AC to DC or in another words: creates absolute value of voltage at the input.
  Transformer: A Triad Magnetics 600Ohm:600Ohm audio transformer.
  DIP - 8 pins: A DIP stand-in part for whatever IC you want. With 8 pins on a 300 mil dual inline package (DIP) footprint.
