# Fritzing sketch Tarjeta Presentacion V1-Min (saved by Fritzing 0.9.3b)
circuit board: 8.55cm x 5.4cm

parts:
  10K = Resistor [tolerance=±5% resistance=220 package=THT]
  part = LED - 3mm [color="Red (633nm)" package="3 mm [THT]"]
  XL = CRYSTAL - kHz [frequency="16 Mhz"]
  22p = Capacitor [package=cap-pth-small-kit]
  22p_2 = Capacitor [package=cap-pth-small-kit]
  0_1u = Ceramic Capacitor [capacitance=100nF package="100 mil [THT, multilayer]"]
  1K = Resistor [tolerance=±5% resistance=220 package=THT]
  part_2 = LED - 3mm [color="Red (633nm)" package="3 mm [THT]"]
  USB = USB+SHIELD [package=usb-b-pth]
  R1 = Resistor [tolerance=±5% resistance=220 package=THT]
  +5V = Battery
  Atmega328P = atmega328 [package=dip]

nets:
  N1: 10K.Pin_0, part_2.anode
  N2: 10K.Pin_1, 0_1u.0, Atmega328P.RESET
  GND: part.cathode, 22p.1, 22p_2.1, 1K.Pin_0, USB.GND, +5V.-, Atmega328P.GND
  N3: part.anode, R1.Pin_0
  N4: XL.pin_0, 22p_2.2, Atmega328P.XLAT1
  N5: XL.pin_1, 22p.2, Atmega328P.XLAT2
  N6: 1K.Pin_1, part_2.cathode
  N7: USB.VBUS, +5V.+
  N8: R1.Pin_1, Atmega328P.D13
  N9: Atmega328P.VCC, Atmega328P.AVCC, Atmega328P.AREF

notes:
  -
  16Mhz
  13 12 11´10´ 9´ 8
  RST 0  1  2  3´ 4  +  -
  5´ 6´ 7  8
  +5Vcc
  GND
  RX TX
  SCL
  SDA
  ArdUn1
  7.6.5
  5V GND TX RX
  -----
  cc
  -1K-
