# Fritzing sketch Vikino (saved by Fritzing 0.9.3b)
circuit board: 6.30446cm x 3.95441cm
breadboards: 2

parts:
  IC1 = MICROCONTROLLER [package=dil28-3]
  XTAL1 = Crystal [frequency="16 Mhz" package=THT]
  C1 = Ceramic Capacitor [capacitance=22pF package="100 mil [THT, multilayer]"]
  C2 = Ceramic Capacitor [capacitance=22pF package="100 mil [THT, multilayer]"]
  Power_plug1 = Power plug
  U1 = Voltage Regulator - 5V [package="TO220 [THT]"]
  C3 = Electrolytic Capacitor [capacitance=100µF package="100 mil [THT, electrolytic]"]
  C4 = Electrolytic Capacitor [capacitance=100µF package="100 mil [THT, electrolytic]"]
  R1 = Resistor [tolerance=±5% resistance=1k package=THT]
  LED1 = LED - 5mm [color="Red (633nm)" package="5 mm [THT]"]
  R2 = Resistor [tolerance=±5% resistance=10k package=THT]
  S1 = Pushbutton [package="[THT]"]
  J1 = female pin header, 8 pins [form="♀ (female)"]
  J2 = female pin header, 4 pins [form="♀ (female)"]
  J3 = female pin header, 14 pins [form="♀ (female)"]
  C5 = Ceramic Capacitor [capacitance=100nF package="100 mil [THT, multilayer]"]
  J4 = female pin header, 6 pins [form="♀ (female)"]
  part = female pin header, 6 pins [form="♀ (female)"]  # not connected
  Power_plug2 = Power plug
  S2 = Toggle Switch [package=THT]

nets:
  N1: IC1.PC6(_RESET), R2.Pin_1, S1.Pin_1, S1.Pin_2, J1.pin1, C5.1
  N2: IC1.PD0(RXD), J1.pin2, J4.pin3
  N3: IC1.PD1(TXD), J1.pin3, J4.pin2
  N4: IC1.PD2(INT0), J1.pin4
  N5: IC1.PD3(INT1), J1.pin5
  N6: IC1.PD4(XCK_T0), J1.pin6
  N7: IC1.VCC, IC1.AVCC, U1.output_voltage, C4.+, R1.Pin_0, R2.Pin_0, J1.pin7, J3.pin6
  GND: IC1.GND, IC1.AGND, C1.1, C2.0, Power_plug1.GND, U1.GND, C3.-, C4.-, LED1.cathode, S1.Pin_3, S1.Pin_4, J1.pin8, J3.pin8, J4.pin6
  N8: IC1.PB6(XTAL1_TOSC1), XTAL1.pin_0, C1.0
  N9: IC1.PB7(XTAL2_TOSC2), XTAL1.pin_1, C2.1
  N10: IC1.PD5(T1), J2.pin1
  N11: IC1.PD6(AIN0), J2.pin2
  N12: IC1.PD7(AIN1), J2.pin3
  N13: IC1.PB0(ICP), J2.pin4
  N14: IC1.PB1(OC1A), J3.pin1
  N15: IC1.PB2(SS_OC1B), J3.pin2
  N16: IC1.PB3(MOSI_OC2), J3.pin3
  N17: IC1.PB4(MISO), J3.pin4
  N18: IC1.PB5(SCK), J3.pin5
  N19: IC1.AREF, J3.pin7
  N20: IC1.PC0(ADC0), J3.pin9
  N21: IC1.PC1(ADC1), J3.pin10
  N22: IC1.PC2(ADC2), J3.pin11
  N23: IC1.PC3(ADC3), J3.pin12
  N24: IC1.PC4(ADC4_SDA), J3.pin13
  N25: IC1.PC5(ADC5_SCL), J3.pin14
  N26: Power_plug1.VCC, U1.input_voltage, C3.+
  N27: R1.Pin_1, LED1.anode
  N28: C5.0, J4.pin1
  N29: Power_plug2.VCC, S2.COM, S2.L2

notes:
  Vikino V1.0
