# Fritzing sketch voltage-regulator_VoltageRegulator_with_switch (saved by Fritzing 0.9.3b)
circuit board: 3.09898cm x 3.10353cm
breadboards: 1

parts:
  S1 = Toggle Switch [package=THT]
  Power_plug1 = Power plug
  J2 = Generic male header - 2 pins [package=THT]
  part = Power plug  # not connected
  C2 = Electrolytic Capacitor [capacitance=1µF package="100 mil [THT, electrolytic]"]
  C1 = Electrolytic Capacitor [capacitance=1µF package="100 mil [THT, electrolytic]"]
  U1 = Voltage Regulator - 5V [package="TO220 [THT]"]

nets:
  N1: S1.COM, C1.+, U1.input_voltage
  N2: S1.L2, Power_plug1.VCC
  GND: Power_plug1.GND, J2.pin2, C2.-, C1.-, U1.GND
  N3: J2.pin1, C2.+, U1.output_voltage

notes:
  Este ejemplo utiliza un regulador de voltaje 7805 para regular el voltaje a 5 voltios. Hay un interruptor para encender y apagar el circuito. La batería debe ser de al menos 7V DC.
