# Fritzing sketch V-1-0-1 (saved by Fritzing 0.9.3b)
breadboards: 1

parts:
  Componente1 = Arduino Uno (Rev3)
  Tiny_RTC1 = Tiny RTC
  Componente2 = DHT22 Module FG
  Componente4 = Bluetooth HC-05 Macho
  Componente25 = FC-28 Soil Hygrometer Module
  Componente26 = Soil Moisture Sensor  # not connected

nets:
  N1: Componente1.A0, Componente25.AO
  GND: Componente1.GND, Tiny_RTC1.GND, Componente2.GND, Componente4.GND, Componente25.GND
  N2: Componente1.A4/SDA, Tiny_RTC1.SDA
  N3: Componente1.A5/SCL, Tiny_RTC1.SCL
  N4: Componente1.D2, Componente2.OUT
  N5: Componente1.D3_PWM, Componente4.VCC
  N6: Componente1.D4, Componente4.Key
  N7: Componente1.D5_PWM, Componente4.TXD
  N8: Componente1.D6_PWM, Componente4.RXD
  VCC: Componente1.5V, Tiny_RTC1.VCC, Componente2.VCC, Componente25.VCC

custom parts:
  Tiny RTC: Tiny RTC I2C module DS1370Z RTC and AT24C32 EEPROM
  DHT22 Module FG: DHT22 module
  FC-28 Soil Hygrometer Module: The FC-28 is a soil hygrometer module that uses the Texas Instruments LM393 comparator chip to provide an analog measurement of soil humidity. The digital output is high when soil moisture is over a certain threshold, as determined by adjusting the potentiometer.

// code stored in the sketch: 1_0_0.ino
/* 
#########################################################
#    Processor:          Arduino UNO, MEGA ou Teensy++ 2.0
#    Language:           Wiring / C /Processing /Fritzing / Arduino IDE
#    Objectives:         Test Module - Tiny RTC DS1307 Z
#    Author:             Andres Felipe Gomez Maya
#    Date:               17/10/2019
#    place:              Medellin, Colombia
#########################################################
#  
#  RTC-I2C: DS:SCL->ARD:SCL  DS:SDA->ARD:SDA  DS:VCC->5V  DS:GND->GND
#           **NOTA**: se debe cargar dos veces este programa 1.Con la linea 9= RTC.adjust(DateTime(__DATE__, __TIME__));
#    
#    
#    
#    
*/

#include <Wire.h> 
#include "RTClib.h"
RTC_DS1307 RTC;
#define A0 A0

void setup () {
  Serial.begin(9600); // Establece la velocidad de datos del puerto serie
  Serial.println("Iniciando el puerto I2C");
  Wire.begin();  
  Serial.println("Abriendo Wire.");.

  if (! RTC.begin()) {
    Serial.println("RTC No Encontrado.");
    while (1);
  }

  if (! RTC.isrunning()) {
    Serial.println("RTC NO funciona!");
  }
  
  // RTC.adjust(DateTime(__DATE__, __TIME__)); // Establece la fecha y hora (Comentar una vez establecida la hora)
} 


void loop(){

  if (! RTC.isrunning()) {
    Serial.println("RTC NO funciona!");
  } else {
    DateTime now = RTC.now(); // Obtiene la fecha y hora del   RTC
    Serial.print(now.year(), DEC); // A§o
    Serial.print('/');
    Serial.print(now.month(), DEC); // Mes
    Serial.print('/');
    Serial.print(now.day(), DEC); // Dia
    Serial.print(' ');
    Serial.print(now.hour(), DEC); // Horas
    Serial.print(':');
    Serial.print(now.minute(), DEC); // Minutos
    Serial.print(':');
    Serial.print(now.second(), DEC); // Segundos
    Serial.println();
  }
}

// code stored in the sketch: test_ds1307z_0.ino
/* 
#########################################################
#    Processor:          Arduino UNO, MEGA ou Teensy++ 2.0
#    Language:           Wiring / C /Processing /Fritzing / Arduino IDE
#    Objectives:         Test Module - Tiny RTC DS1307 Z
#    Author:             Andres Felipe Gomez Maya
#    Date:               17/10/2019
#    place:              Medellin, Colombia
#########################################################
*/

//  Prueba de Reloj Tiempo Real (RTC) y Modulo I2C
//  Conexion:
//    Arduino UNO  SCL->SCL  SDA->SDA  VCC->5V  GND->GND
//  
//    NOTA: se debe cargar dos veces este programa 1.Con la linea 9= RTC.adjust(DateTime(__DATE__, __TIME__));

#include <Wire.h> 
#include "RTClib.h"
RTC_DS1307 RTC;

void setup () {
  Serial.begin(9600); // Establece la velocidad de datos del puerto serie
  Serial.println("Inicia el puerto I2C");
  
  Serial.println("Abriendo Wire.");
  Wire.begin(); // 
  
  Serial.println("RTC Begin.");
  RTC.begin(); // Inicia la comunicaci?n con el RTC
  // RTC.adjust(DateTime(__DATE__, __TIME__)); // Establece la fecha y hora (Comentar una vez establecida la hora)
}
void loop(){
  DateTime now = RTC.now(); // Obtiene la fecha y hora del RTC
  Serial.print(now.year(), DEC); // A?o
  Serial.print('/');
  Serial.print(now.month(), DEC); // Mes
  Serial.print('/');
  Serial.print(now.day(), DEC); // Dia
  Serial.print(' ');
  Serial.print(now.hour(), DEC); // Horas
  Serial.print(':');
  Serial.print(now.minute(), DEC); // Minutos
  Serial.print(':');
  Serial.print(now.second(), DEC); // Segundos
  Serial.println();
}
