# Fritzing sketch double_plant_watering_vNzVaaYbCH (saved by Fritzing 0.9.3b)
breadboards: 1

parts:
  Q1 = NPN-Transistor [part_number=bc368 package="TO92 [THT]"]
  Q2 = NPN-Transistor [part_number=bc368 package="TO92 [THT]"]
  D1 = Rectifier Diode [part_number=1N4001 package="300 mil [THT]"]
  D2 = Rectifier Diode [part_number=1N4001 package="300 mil [THT]"]
  R1 = Resistor [tolerance=±5% resistance=1k package=THT]
  R2 = Resistor [tolerance=±5% resistance=1k package=THT]
  C1 = Electrolytic Capacitor [capacitance=1mF package="100 mil [THT, electrolytic]"]
  M1 = DC Motor [part_number=Pump11]
  M2 = DC Motor [part_number=pump2]
  V1 = DC Power [voltage=5]
  Componente1 = Arduino Pro Mini (5V)
  D3 = Rectifier Diode [part_number=1N4001 package="300 mil [THT]"]

nets:
  N1: Q1.E, Q2.E, C1.-, V1.V-, Componente1.GND
  N2: Q1.B, R1.Pin_1
  N3: Q1.C, D2.anode, M1.pin_2
  N4: Q2.B, R2.Pin_1
  N5: Q2.C, D1.anode, M2.pin_2
  N6: D1.cathode, D2.cathode, C1.+, M1.pin_1, M2.pin_1, V1.V+, D3.anode
  N7: R1.Pin_0, Componente1.D7
  N8: R2.Pin_0, Componente1.D8
  N9: Componente1.VCC, D3.cathode
