# Fritzing sketch wateringsystem_IX37ZrM4hZ (saved by Fritzing 0.9.3b)
breadboards: 1

parts:
  Part1 = Arduino Uno (Rev3)
  ZS-042_RTC1 = ZS-042 RTC Module
  U1 = Tri-Color LED SMD [package=led-tricolor-smd]
  Water_Flow_Sensor = female pin header, 3 pins [form="♀ (female)"]
  S1 = Round Pushbutton
  S2 = Round Pushbutton
  Part2 = MOSFET4
  12V_Supply = female pin header, 2 pins [form="♀ (female)"]

nets:
  N1: Part1.A0, U1.GRN
  N2: Part1.A1, U1.RED
  N3: Part1.A2, U1.BLU
  N4: Part1.A4/SDA, ZS-042_RTC1.SDA
  N5: Part1.A5/SCL, ZS-042_RTC1.SCL
  N6: Part1.D8, ZS-042_RTC1.SQW
  N7: Part1.D10_PWM/SS, S1.leg1
  N8: Part1.D11_PWM/MOSI, S2.leg1
  N9: Part1.D12/MISO, Water_Flow_Sensor.pin2
  N10: Part1.D4, Part2.IN1
  N11: Part1.D5_PWM, Part2.IN2
  N12: Part1.D6_PWM, Part2.IN3
  N13: Part1.D7, Part2.IN4
  5V: Part1.5V, ZS-042_RTC1.VCC, Water_Flow_Sensor.pin3
  GND: Part1.GND, ZS-042_RTC1.GND, U1.A, Water_Flow_Sensor.pin1, S1.leg0, S2.leg0, Part2.GND, 12V_Supply.pin2
  VIN: Part1.VIN, Part2.VCC, 12V_Supply.pin1

custom parts:
  Round Pushbutton: A generic black pushbutton.
  Round Pushbutton: A generic black pushbutton.
  MOSFET4: 4 Channel MOSFET
