# Fritzing sketch MVLTDAV2 (saved by Fritzing 0.9.3b)
circuit board: 8.55cm x 5.4cm
breadboards: 1

parts:
  +1 = Rectifier Diode [part_number=1N4001 package="300 mil [THT]"]
  1K1 = Resistor [tolerance=±5% resistance=220 package=THT]
  1 = LED - 3mm [color="Red (633nm)" package="3 mm [THT]"]
  LDR1 = Capacitor [package=cap-pth-small-kit]
  100k1 = Resistor [tolerance=±5% resistance=220 package=THT]
  0_1u1 = Ceramic Capacitor [capacitance=100nF package="100 mil [THT, multilayer]"]
  Atmega328P1 = atmega328 [package=dip]
  10K1 = Resistor [tolerance=±5% resistance=220 package=THT]
  XL1 = CRYSTAL - kHz [frequency="16 Mhz"]
  +5V1 = Battery
  22p1 = Capacitor [package=cap-pth-small-kit]
  22p2 = Capacitor [package=cap-pth-small-kit]
  -_+1 = Rectifier Diode [part_number=1N4001 package="300 mil [THT]"]
  USB1 = USB+SHIELD [package=usb-b-pth]
  RGB1 = RGB LED - (4 legs) [package="5 mm [THT]"]
  1K2 = Resistor [tolerance=±5% resistance=220 package=THT]
  P1 = female pin header, 6 pins [form="♀ (female)"]
  J1 = female pin header, 6 pins [form="♀ (female)"]
  J2 = female pin header, 4 pins [form="♀ (female)"]
  J3 = female pin header, 5 pins [form="♀ (female)"]

nets:
  N1: +1.cathode, 1.anode, 100k1.Pin_0, Atmega328P1.VCC, Atmega328P1.AVCC, Atmega328P1.AREF, 10K1.Pin_0, -_+1.cathode
  GND: 1K1.Pin_0, LDR1.2, Atmega328P1.GND, Atmega328P1.XLAT1, XL1.pin_0, +5V1.+, 22p1.1, 22p1.2, 22p2.1, USB1.GND
  N2: 1K1.Pin_1, 1.cathode
  N3: LDR1.1, 100k1.Pin_1
  N4: 0_1u1.0, Atmega328P1.RESET, 10K1.Pin_1
  N5: Atmega328P1.D0_(RX), J3.pin1
  N6: Atmega328P1.D1_(TX), J3.pin2
  N7: Atmega328P1.D2, J3.pin3
  N8: Atmega328P1.D3_(PWM), J3.pin4
  N9: Atmega328P1.D4, J3.pin5
  N10: Atmega328P1.XLAT2, XL1.pin_1, 22p2.2
  N11: Atmega328P1.D5_(PWM), RGB1.blue_cathode, J2.pin1
  N12: Atmega328P1.D6_(PWM), RGB1.green_cathode, J2.pin2
  N13: Atmega328P1.D7, RGB1.red_cathode, J2.pin3
  N14: Atmega328P1.D8, J1.pin6, J2.pin4
  N15: Atmega328P1.D9_(PWM), J1.pin5
  N16: Atmega328P1.D10_(PWM), J1.pin4
  N17: Atmega328P1.D11_(PWM), J1.pin3
  N18: Atmega328P1.D12, J1.pin2
  N19: Atmega328P1.D13, J1.pin1
  N20: Atmega328P1.A0, P1.pin6
  N21: Atmega328P1.A1, P1.pin5
  N22: Atmega328P1.A2, P1.pin4
  N23: Atmega328P1.A3, P1.pin3
  N24: Atmega328P1.A4, P1.pin2
  N25: Atmega328P1.A5, P1.pin1
  N26: +5V1.-, -_+1.anode, USB1.VBUS
  N27: RGB1.common_anode, 1K2.Pin_0

notes:
  SISPRA REV - FelipheGomez
  Monteverde LTDA
  Fb:monteverdeforestalyambiental
  www.monteverdeltda.com
  Create by FelipheGomez
  5V GND TX RX
  instagram:monteverde_ambiental
  -
  cc
  -----
  .
  ----- Ardu5 -----
  GND
  -1K-
  16Mhz
  SDA
  SCL
  RX TX
  +5Vcc
  5´ 6´ 7  8
  RST 0  1  2  3´ 4  +  -
  13 12 11´10´ 9´ 8
  Arduino UNO FelipheGomez
  A5 A4 A3 A2 A1 A0
  7.6.5
