# Fritzing sketch 0.1 (saved by Fritzing 0.9.3b)
circuit board: 16.9333cm x 5.64444cm
breadboards: 1

parts:
  U1 = atmega328 [package=dip]
  U2 = Voltage Regulator - 5V [package="DPak [SMD]"]
  C1 = Electrolytic Capacitor [capacitance=100μF package="0807 [SMD, electrolytic]"]
  C2 = Electrolytic Capacitor [capacitance=100μF package="0807 [SMD, electrolytic]"]
  S1 = Pushbutton [package="[THT]"]
  XTAL1 = CRYSTAL - kHz [frequency="16 Mhz"]
  C3 = Ceramic Capacitor [capacitance=22µF voltage=10V package="100 mil [THT, multilayer]"]
  C4 = Ceramic Capacitor [capacitance=22µF voltage=10V package="100 mil [THT, multilayer]"]
  Power_plug1 = Power plug
  R1 = Resistor [tolerance=±5% resistance=10k package=THT]
  R2 = Resistor [tolerance=±5% resistance=220 package=THT]
  LED1 = LED - 5mm [color="Red (633nm)" package="5 mm [THT]"]
  LED2 = LED - 5mm [color="Red (633nm)" package="5 mm [THT]"]
  R3 = Resistor [tolerance=±5% resistance=680 package=THT]
  part = LED - 5mm [color="Red (633nm)" package="5 mm [THT]"]  # not connected

nets (from the breadboard view):
  N1: U1.RESET, S1.Pin_1, S1.Pin_2
  N2: U1.VCC, U1.AVCC, U1.AREF, U2.output_voltage, C2.+, R1.Pin_1, R2.Pin_0
  GND: U1.GND, U2.GND, C1.-, C2.-, S1.Pin_3, S1.Pin_4, C3.0, C4.1, Power_plug1.GND, LED1.anode, R3.Pin_0
  N3: U1.XLAT1, XTAL1.pin_0, C3.1
  N4: U1.XLAT2, XTAL1.pin_1, C4.0
  N5: U1.D13, LED2.cathode
  N6: U2.input_voltage, C1.+, Power_plug1.VCC
  N7: R2.Pin_1, LED1.cathode
  N8: LED2.anode, R3.Pin_1
