# Fritzing sketch 2 (saved by Fritzing 0.9.3b)
breadboards: 1

parts:
  R1 = Resistor [tolerance=±5% resistance=10k package=THT]
  C1 = Ceramic Capacitor [capacitance=22pF package="100 mil [THT, multilayer]"]
  Xtal1 = CRYSTAL - kHz [frequency="16 Mhz"]
  C2 = Ceramic Capacitor [capacitance=22pF package="100 mil [THT, multilayer]"]
  R2 = Resistor [tolerance=±5% resistance=560 package=THT]
  LED1 = LED - 5mm [color="Red (633nm)" package="5 mm [THT]"]
  D1 = Rectifier Diode [part_number=1N5059 package="300 mil [THT]"]
  D2 = Rectifier Diode [part_number=1N5059 package="300 mil [THT]"]
  D3 = Rectifier Diode [part_number=1N5059 package="300 mil [THT]"]
  D4 = Rectifier Diode [part_number=1N5059 package="300 mil [THT]"]
  C3 = Electrolytic Capacitor [capacitance=1mF package="100 mil [THT, electrolytic]"]
  C4 = Ceramic Capacitor [capacitance=100nF package="100 mil [THT, multilayer]"]
  D5 = Rectifier Diode [part_number=1N4001 package="300 mil [THT]"]
  C5 = Electrolytic Capacitor [capacitance=1µF package="100 mil [THT, electrolytic]"]
  C6 = Ceramic Capacitor [capacitance=100nF package="100 mil [THT, multilayer]"]
  LED2 = LED - 5mm [color="Green (565nm)" package="5 mm [THT]"]
  R3 = Resistor [tolerance=±5% resistance=470 package=THT]
  IC2 = LM7805 [package=TO-220]
  IC1 = ATmega 328P [package=dip]
  12v_- = female pin header, 4 pins [form="♀ (female)"]
  12v_+ = female pin header, 4 pins [form="♀ (female)"]
  GND = female pin header, 5 pins [form="♀ (female)"]
  5v+ = female pin header, 5 pins [form="♀ (female)"]
  J1 = Screw terminal - 2 pins [package=THT]
  ANALG = female pin header, 6 pins [form="♀ (female)"]
  D5-D8 = female pin header, 4 pins [form="♀ (female)"]
  D0-D4 = female pin header, 5 pins [form="♀ (female)"]
  D13-D9 = female pin header, 5 pins [form="♀ (female)"]

nets:
  N1: R1.Pin_0, LED1.anode, D5.anode, C5.+, C6.0, LED2.anode, IC2.OUT, IC1.VCC, IC1.AVCC, 5v+.pin1, 5v+.pin2, 5v+.pin3, 5v+.pin4, 5v+.pin5
  N2: R1.Pin_1, IC1.PC6_(PCINT14/^RESET)_[RESET]
  GND: C1.0, C2.1, D3.anode, D4.anode, C3.-, C4.1, C5.-, C6.1, R3.Pin_1, IC2.GND, IC1.GND, GND.pin1, GND.pin2, GND.pin3, GND.pin4, GND.pin5
  N3: C1.1, Xtal1.pin_1, IC1.PB6_(PCINT6/XTAL1/TOSC1)_[XTAL1]
  N4: Xtal1.pin_0, C2.0, IC1.PB7_(PCINT7/XTAL2/TOSC2)_[XTAL2]
  N5: R2.Pin_0, IC1.PB5_(SCK/PCINT5)_[D13], D13-D9.pin1
  N6: R2.Pin_1, LED1.cathode
  N7: D1.cathode, D2.cathode, C3.+, C4.0, D5.cathode, IC2.IN
  N8: D1.anode, D3.cathode, 12v_-.pin1, 12v_-.pin2, 12v_-.pin3, 12v_-.pin4, J1.pin2
  N9: D2.anode, D4.cathode, 12v_+.pin1, 12v_+.pin2, 12v_+.pin3, 12v_+.pin4, J1.pin1
  N10: LED2.cathode, R3.Pin_0
  N11: IC1.PD0_(PCINT16/RXD)_[D0], D0-D4.pin1
  N12: IC1.PD1_(PCINT17/TXD)_[D1], D0-D4.pin2
  N13: IC1.PD2_(PCINT18/INT0)_[D2], D0-D4.pin3
  N14: IC1.PD3_(PCINT19/OC2B/INT1)_[D3_PWM], D0-D4.pin4
  N15: IC1.PD4_(PCINT20/XCK/T0)_[D4], D0-D4.pin5
  N16: IC1.PD5_(PCINT21/OC0B/T1)_[D5_PWM], D5-D8.pin1
  N17: IC1.PD6_(PCINT22/OC0A/AIN0)_[D6_PWM], D5-D8.pin2
  N18: IC1.PD7_(PCINT23/AIN1)_[D7], D5-D8.pin3
  N19: IC1.PB0_(PCINT0/CLK0/ICP1)_[D8], D5-D8.pin4
  N20: IC1.PB1_(OC1A/PCINT1)_[D9_PWM], D13-D9.pin5
  N21: IC1.PB2_(^SS/OC1B/PCINT2)_[D10_PWM], D13-D9.pin4
  N22: IC1.PB3_(MOSI/OC2A/PCINT3)_[D11_PWM], D13-D9.pin3
  N23: IC1.PB4_(MISO/PCINT4)_[D12], D13-D9.pin2
  N24: IC1.PC0_(ADC0/PCINT8)_[A0], ANALG.pin1
  N25: IC1.PC1_(ADC1/PCINT9)_[A1], ANALG.pin2
  N26: IC1.PC2_(ADC2/PCINT10)_[A2], ANALG.pin3
  N27: IC1.PC3_(ADC3/PCINT11)_[A3], ANALG.pin4
  N28: IC1.PC4_(ADC4/SDA/PCINT12)_[A4], ANALG.pin5
  N29: IC1.PC5_(ADC5/SCL/PCINT13)_[A5], ANALG.pin6

custom parts:
  LM7805: LM 7805 Voltage Regulator
  ATmega 328P: Atmel ATmega 328P-PU Microcontroller
