# Fritzing sketch 2r (saved by Fritzing 0.9.3b)
breadboards: 1

parts:
  R1 = Resistor [tolerance=±5% resistance=10k package=THT]
  C1 = Ceramic Capacitor [capacitance=22pF package="100 mil [THT, multilayer]"]
  Xtal1 = CRYSTAL - kHz [frequency="16 Mhz"]
  C2 = Ceramic Capacitor [capacitance=22pF package="100 mil [THT, multilayer]"]
  R2 = Resistor [tolerance=±5% resistance=560 package=THT]
  LED1 = LED - 5mm [color="Red (633nm)" package="5 mm [THT]"]
  D1 = Rectifier Diode [part_number=1N5059 package="300 mil [THT]"]
  D2 = Rectifier Diode [part_number=1N5059 package="300 mil [THT]"]
  D3 = Rectifier Diode [part_number=1N5059 package="300 mil [THT]"]
  D4 = Rectifier Diode [part_number=1N5059 package="300 mil [THT]"]
  C3 = Electrolytic Capacitor [capacitance=1mF package="100 mil [THT, electrolytic]"]
  C4 = Ceramic Capacitor [capacitance=100nF package="100 mil [THT, multilayer]"]
  D5 = Rectifier Diode [part_number=1N4001 package="300 mil [THT]"]
  C5 = Electrolytic Capacitor [capacitance=1µF package="100 mil [THT, electrolytic]"]
  C6 = Ceramic Capacitor [capacitance=100nF package="100 mil [THT, multilayer]"]
  LED2 = LED - 5mm [color="Green (565nm)" package="5 mm [THT]"]
  R3 = Resistor [tolerance=±5% resistance=470 package=THT]
  12v_- = female pin header, 4 pins [form="♀ (female)"]
  12v_+ = female pin header, 4 pins [form="♀ (female)"]
  5v_+ = female pin header, 5 pins [form="♀ (female)"]
  5v_GND = female pin header, 5 pins [form="♀ (female)"]
  J1 = Screw terminal - 2 pins [package=THT]

nets:
  N1: R1.Pin_0, LED1.anode, D5.anode, C5.+, C6.0, LED2.anode, 5v_GND.pin1, 5v_GND.pin2, 5v_GND.pin3, 5v_GND.pin4, 5v_GND.pin5
  N2: C1.0, C2.1, D3.anode, D4.anode, C3.-, C4.1, C5.-, C6.1, R3.Pin_1, 5v_+.pin1, 5v_+.pin2, 5v_+.pin3, 5v_+.pin4, 5v_+.pin5
  N3: C1.1, Xtal1.pin_1
  N4: Xtal1.pin_0, C2.0
  N5: R2.Pin_1, LED1.cathode
  N6: D1.cathode, D2.cathode, C3.+, C4.0, D5.cathode
  N7: D1.anode, D3.cathode, 12v_-.pin1, 12v_-.pin2, 12v_-.pin3, 12v_-.pin4, J1.pin2
  N8: D2.anode, D4.cathode, 12v_+.pin1, 12v_+.pin2, 12v_+.pin3, 12v_+.pin4, J1.pin1
  N9: LED2.cathode, R3.Pin_0
