# Fritzing sketch base (saved by Fritzing 0.9.3b)
breadboards: 1

parts:
  R1 = Resistor [tolerance=±5% resistance=10k package=THT]
  C1 = Ceramic Capacitor [capacitance=22pF package="100 mil [THT, multilayer]"]
  Xtal1 = CRYSTAL - kHz [frequency="16 Mhz"]
  C2 = Ceramic Capacitor [capacitance=22pF package="100 mil [THT, multilayer]"]
  R2 = Resistor [tolerance=±5% resistance=560 package=THT]
  LED1 = LED - 5mm [color="Red (633nm)" package="5 mm [THT]"]
  J1 = Screw terminal - 2 pins [package=THT]
  D1 = Rectifier Diode [part_number=1N5059 package="300 mil [THT]"]
  D2 = Rectifier Diode [part_number=1N5059 package="300 mil [THT]"]
  D3 = Rectifier Diode [part_number=1N5059 package="300 mil [THT]"]
  D4 = Rectifier Diode [part_number=1N5059 package="300 mil [THT]"]
  C3 = Electrolytic Capacitor [capacitance=1mF package="100 mil [THT, electrolytic]"]
  C4 = Ceramic Capacitor [capacitance=100nF package="100 mil [THT, multilayer]"]
  D5 = Rectifier Diode [part_number=1N4001 package="300 mil [THT]"]
  C5 = Electrolytic Capacitor [capacitance=1µF package="100 mil [THT, electrolytic]"]
  C6 = Ceramic Capacitor [capacitance=100nF package="100 mil [THT, multilayer]"]
  LED2 = LED - 5mm [color="Green (565nm)" package="5 mm [THT]"]
  R3 = Resistor [tolerance=±5% resistance=470 package=THT]
  IC2 = LM7805 [package=TO-220]
  IC1 = ATmega 328P [package=dip]

nets:
  N1: R1.Pin_0, LED1.anode, D5.anode, C5.+, C6.0, LED2.anode, IC2.OUT, IC1.VCC, IC1.AVCC
  N2: R1.Pin_1, IC1.PC6_(PCINT14/^RESET)_[RESET]
  GND: C1.0, C2.1, D3.anode, D4.anode, C3.-, C4.1, C5.-, C6.1, R3.Pin_1, IC2.GND, IC1.GND
  N3: C1.1, Xtal1.pin_1, IC1.PB6_(PCINT6/XTAL1/TOSC1)_[XTAL1]
  N4: Xtal1.pin_0, C2.0, IC1.PB7_(PCINT7/XTAL2/TOSC2)_[XTAL2]
  N5: R2.Pin_0, IC1.PB5_(SCK/PCINT5)_[D13]
  N6: R2.Pin_1, LED1.cathode
  N7: J1.pin1, D2.anode, D4.cathode
  N8: J1.pin2, D1.anode, D3.cathode
  N9: D1.cathode, D2.cathode, C3.+, C4.0, D5.cathode, IC2.IN
  N10: LED2.cathode, R3.Pin_0

custom parts:
  LM7805: LM 7805 Voltage Regulator
  ATmega 328P: Atmel ATmega 328P-PU Microcontroller
