# Fritzing sketch 000002 (saved by Fritzing 0.9.3b)
circuit board: 6.83702cm x 5.31663cm
perfboards: 1

parts:
  Componente1 = Arduino Uno (Rev3)
  Componente4 = Bluetooth HC-05 Macho
  Componente5 = FC-28 Soil Hygrometer Module
  Componente7 = FC-28 Soil Hygrometer Module - Probe
  Water_Level_Sensor1 = Water Level Sensor
  VALVE1 = Plastic Solenoid Valve
  J3 = Power Jack [package=power_jack_pth_lock]
  KY-1 = Keyes Relay [package=THT]
  KY-2 = Keyes Relay [package=THT]
  LED3 = LEDs [package=led10mm]
  Componente2 = DHT22 Module FG
  Power_plug1 = Power plug
  Power_plug2 = Power plug
  Power_plug3 = Power plug
  Power_plug4 = Power plug
  X1 = USB Connectors [package=usb-a-pcb]
  X2 = USB Connectors [package=usb-a-h]
  X3 = USB Connectors [package=usb-a-pcb]
  X4 = USB Connectors [package=usb-a-h]
  J4 = Piezo Speaker

nets:
  N1: Componente1.A0, X3.D+
  N2: Componente1.A1, X1.D+
  N3: Componente1.D8, KY-1.signal
  N4: Componente1.D9_PWM, KY-2.signal
  GND: Componente1.GND, Componente4.GND, J3.GND, KY-1.ground, KY-2.ground, Componente2.GND, Power_plug2.GND, Power_plug3.GND, X1.GND, X3.GND, J4.pin1
  N5: Componente1.D2, Componente2.OUT
  N6: Componente1.D3_PWM, Componente4.VCC
  N7: Componente1.D4, Componente4.Key
  N8: Componente1.D5_PWM, Componente4.TXD
  N9: Componente1.D6_PWM, Componente4.RXD
  N10: Componente1.D7, J4.pin2
  5V: Componente1.5V, KY-1.power, KY-2.power, Componente2.VCC, X1.VBUS, X3.VBUS
  VIN: Componente1.VIN, J3.PWR, KY-1.C, KY-2.NC, KY-2.C, KY-2.NO, Power_plug2.VCC
  N11: Componente5.VCC, X4.VBUS
  GND_2: Componente5.GND, X4.GND
  N12: Componente5.AO, X4.D+
  N13: Componente5.POS, Componente7.POS
  N14: Componente5.NEG, Componente7.NEG
  N15: Water_Level_Sensor1.SIG, X2.D+
  N16: Water_Level_Sensor1.VCC, X2.VBUS
  GND_3: Water_Level_Sensor1.GND, X2.GND
  N17: VALVE1.no_name_yet#1, Power_plug1.VCC
  N18: VALVE1.no_name_yet#2, Power_plug1.GND
  N19: KY-1.NO, Power_plug3.VCC
  N20: LED3.C, Power_plug4.GND
  N21: LED3.A, Power_plug4.VCC

custom parts:
  FC-28 Soil Hygrometer Module: The FC-28 is a soil hygrometer module that uses the Texas Instruments LM393 comparator chip to provide an analog measurement of soil humidity. The digital output is high when soil moisture is over a certain threshold, as determined by adjusting the potentiometer.
  FC-28 Soil Hygrometer Module - Probe: The FC-28 is a soil hygrometer module that uses the Texas Instruments LM393 comparator chip to provide an analog measurement of soil humidity.
  Water Level Sensor: A water level sensor. This sensor operates at 3V to 5V. The Sig (signal) pin outputs an analogue signal that is in proportion to the amount of water in contact with the sensor.
  Keyes Relay: The Keyes 5V relay module is suitable for SCM development, home appliance control. It uses a 5V~12V TIL control signal which can control DC / AC signal.
  DHT22 Module FG: DHT22 module

// code stored in the sketch: 1_0_0.ino
/* 
#########################################################
#    Processor:          Arduino UNO, MEGA ou Teensy++ 2.0
#    Language:           Wiring / C /Processing /Fritzing / Arduino IDE
#    Objectives:         Test Module - Tiny RTC DS1307 Z
#    Author:             Andres Felipe Gomez Maya
#    Date:               17/10/2019
#    place:              Medellin, Colombia
#########################################################
#  
#  RTC-I2C: DS:SCL->ARD:SCL  DS:SDA->ARD:SDA  DS:VCC->5V  DS:GND->GND
#           **NOTA**: se debe cargar dos veces este programa 1.Con la linea 9= RTC.adjust(DateTime(__DATE__, __TIME__));
#    
#    
#    
#    
*/

#include <Wire.h> 
#include "RTClib.h"
RTC_DS1307 RTC;
#define A0 A0

void setup () {
  Serial.begin(9600); // Establece la velocidad de datos del puerto serie
  Serial.println("Iniciando el puerto I2C");
  Wire.begin();  
  Serial.println("Abriendo Wire.");.

  if (! RTC.begin()) {
    Serial.println("RTC No Encontrado.");
    while (1);
  }

  if (! RTC.isrunning()) {
    Serial.println("RTC NO funciona!");
  }
  
  // RTC.adjust(DateTime(__DATE__, __TIME__)); // Establece la fecha y hora (Comentar una vez establecida la hora)
} 


void loop(){

  if (! RTC.isrunning()) {
    Serial.println("RTC NO funciona!");
  } else {
    DateTime now = RTC.now(); // Obtiene la fecha y hora del   RTC
    Serial.print(now.year(), DEC); // A§o
    Serial.print('/');
    Serial.print(now.month(), DEC); // Mes
    Serial.print('/');
    Serial.print(now.day(), DEC); // Dia
    Serial.print(' ');
    Serial.print(now.hour(), DEC); // Horas
    Serial.print(':');
    Serial.print(now.minute(), DEC); // Minutos
    Serial.print(':');
    Serial.print(now.second(), DEC); // Segundos
    Serial.println();
  }
}

// code stored in the sketch: test_ds1307z_0.ino
/* 
#########################################################
#    Processor:          Arduino UNO, MEGA ou Teensy++ 2.0
#    Language:           Wiring / C /Processing /Fritzing / Arduino IDE
#    Objectives:         Test Module - Tiny RTC DS1307 Z
#    Author:             Andres Felipe Gomez Maya
#    Date:               17/10/2019
#    place:              Medellin, Colombia
#########################################################
*/

//  Prueba de Reloj Tiempo Real (RTC) y Modulo I2C
//  Conexion:
//    Arduino UNO  SCL->SCL  SDA->SDA  VCC->5V  GND->GND
//  
//    NOTA: se debe cargar dos veces este programa 1.Con la linea 9= RTC.adjust(DateTime(__DATE__, __TIME__));

#include <Wire.h> 
#include "RTClib.h"
RTC_DS1307 RTC;

void setup () {
  Serial.begin(9600); // Establece la velocidad de datos del puerto serie
  Serial.println("Inicia el puerto I2C");
  
  Serial.println("Abriendo Wire.");
  Wire.begin(); // 
  
  Serial.println("RTC Begin.");
  RTC.begin(); // Inicia la comunicaci?n con el RTC
  // RTC.adjust(DateTime(__DATE__, __TIME__)); // Establece la fecha y hora (Comentar una vez establecida la hora)
}
void loop(){
  DateTime now = RTC.now(); // Obtiene la fecha y hora del RTC
  Serial.print(now.year(), DEC); // A?o
  Serial.print('/');
  Serial.print(now.month(), DEC); // Mes
  Serial.print('/');
  Serial.print(now.day(), DEC); // Dia
  Serial.print(' ');
  Serial.print(now.hour(), DEC); // Horas
  Serial.print(':');
  Serial.print(now.minute(), DEC); // Minutos
  Serial.print(':');
  Serial.print(now.second(), DEC); // Segundos
  Serial.println();
}
