# Fritzing sketch ArduinoISP - Programmer - PCB (saved by Fritzing 0.9.3b)
circuit board: 6.88566cm x 5.36311cm
breadboards: 2

parts:
  RESET = Pushbutton [package="[THT]"]
  R6 = Resistor [resistance=220 tolerance=±5% package=THT]
  R7 = Resistor [resistance=220 tolerance=±5% package=THT]
  R8 = Resistor [resistance=220 tolerance=±5% package=THT]
  R9 = Resistor [resistance=220 tolerance=±5% package=THT]
  R10 = Resistor [resistance=1k tolerance=±5% package=THT]
  Arduino1 = Arduino Uno (Rev3)
  ATMEGA = atmega168 [package=dip]
  XTAL = Crystal [frequency="16 Mhz" package=THT]
  C1 = Ceramic Capacitor [capacitance=22pF package="100 mil [THT, multilayer]"]
  C2 = Ceramic Capacitor [capacitance=22pF package="100 mil [THT, multilayer]"]
  H3LL0 = LED - 3mm [color="Green (555nm)" package="3 mm [THT]"]
  PROG = LED - 3mm [color="Yellow (585nm)" package="3 mm [THT]"]
  ERROR = LED - 3mm [color="Red (633nm)" package="3 mm [THT]"]
  PULSE = LED - 3mm [color="Green (555nm)" package="3 mm [THT]"]

nets:
  N1: RESET.Pin_1, RESET.Pin_2, R10.Pin_1, Arduino1.D10_PWM/SS, ATMEGA.RESET
  GND: RESET.Pin_3, RESET.Pin_4, R6.Pin_0, R7.Pin_1, R8.Pin_1, R9.Pin_1, Arduino1.GND, ATMEGA.GND, C1.1, C2.0
  N2: R6.Pin_1, H3LL0.cathode
  N3: R7.Pin_0, PULSE.cathode
  N4: R8.Pin_0, ERROR.cathode
  N5: R9.Pin_0, PROG.cathode
  5V: R10.Pin_0, Arduino1.5V, ATMEGA.VCC, ATMEGA.AVCC
  N6: Arduino1.D8, ERROR.anode
  N7: Arduino1.D9_PWM, PULSE.anode
  N8: Arduino1.D11_PWM/MOSI, ATMEGA.D11_(PWM)
  N9: Arduino1.D12/MISO, ATMEGA.D12
  N10: Arduino1.D13/SCK, ATMEGA.D13
  N11: Arduino1.D7, PROG.anode
  N12: ATMEGA.XLAT1, XTAL.pin_0, C1.0
  N13: ATMEGA.XLAT2, XTAL.pin_1, C2.1
  N14: ATMEGA.D8, H3LL0.anode
