# Fritzing sketch ArduinoISP - Programmer - PCB2 (saved by Fritzing 0.9.3b)
circuit board: 6.88566cm x 5.36311cm
breadboards: 1

parts:
  RESET = Pushbutton [package="[THT]"]
  R6 = Resistor [resistance=220 tolerance=±5% package=THT]
  R7 = Resistor [resistance=220 tolerance=±5% package=THT]
  R8 = Resistor [resistance=220 tolerance=±5% package=THT]
  R9 = Resistor [resistance=220 tolerance=±5% package=THT]
  R10 = Resistor [resistance=1k tolerance=±5% package=THT]
  Arduino1 = Arduino Uno (Rev3)
  ATMEGA = atmega168 [package=dip]
  XTAL = Crystal [frequency="16 Mhz" package=THT]
  C2 = Ceramic Capacitor [capacitance=22pF package="100 mil [THT, multilayer]"]
  H3LL0 = LED - 3mm [color="Green (555nm)" package="3 mm [THT]"]
  PROG = LED - 3mm [color="Yellow (585nm)" package="3 mm [THT]"]
  ERROR = LED - 3mm [color="Red (633nm)" package="3 mm [THT]"]
  PULSE = LED - 3mm [color="Green (555nm)" package="3 mm [THT]"]
  C1 = Ceramic Capacitor [capacitance=22pF package="100 mil [THT, multilayer]"]
  Componente2 = Adafruit Proto Shield R3 [part_number="Adafruit #2077"]  # not connected
  J1 = female pin header, 5 pins [form="♀ (female)"]  # not connected
  J2 = female pin header, 5 pins [form="♀ (female)"]  # not connected
  Digital_I/0-7 = female pin header, 8 pins [form="♀ (female)"]
  J4 = female pin header, 8 pins [form="♀ (female)"]
  Digital_I/0-12 = female pin header, 10 pins [form="♀ (female)"]

nets:
  N1: RESET.Pin_1, RESET.Pin_2, R10.Pin_1, Arduino1.D10_PWM/SS, ATMEGA.RESET
  GND: RESET.Pin_3, RESET.Pin_4, R6.Pin_0, R7.Pin_1, R8.Pin_1, R9.Pin_1, Arduino1.GND, ATMEGA.GND, C2.0, C1.1, J4.pin2
  N2: R6.Pin_1, H3LL0.cathode
  N3: R7.Pin_0, PULSE.cathode
  N4: R8.Pin_0, ERROR.cathode
  N5: R9.Pin_0, PROG.cathode
  5V: R10.Pin_0, Arduino1.5V, ATMEGA.VCC, ATMEGA.AVCC
  N6: Arduino1.D8, ERROR.anode, Digital_I/0-12.pin1
  N7: Arduino1.D9_PWM, PULSE.anode
  N8: Arduino1.D11_PWM/MOSI, ATMEGA.D11_(PWM)
  N9: Arduino1.D12/MISO, ATMEGA.D12
  N10: Arduino1.D13/SCK, ATMEGA.D13
  N11: Arduino1.D7, PROG.anode, Digital_I/0-7.pin8
  N12: ATMEGA.XLAT1, XTAL.pin_0, C1.0
  N13: ATMEGA.XLAT2, XTAL.pin_1, C2.1
  N14: ATMEGA.D8, H3LL0.anode

custom parts:
  Adafruit Proto Shield R3: This prototyping shield is the best out there (well, we think so, at least), and now is even better with Version R3 - updated for the most compatibility with just about all the Arduinos! It works with UNO, Mega, Leonardo, NG, Diecimila, Duemilanove, and compatible Arduinos. Yun's and Arduino Ethernets have a chunky Ethernet jack that gets in the way of stacking, you can use the stacking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
