# Fritzing sketch ArduinoISP - Programmer (saved by Fritzing 0.9.3b)
circuit board: 6.88566cm x 5.36311cm
breadboards: 2

parts:
  RESET = Pushbutton [package="[THT]"]
  R6 = Resistor [resistance=220 tolerance=±5% package=THT]
  PROG = LED - 5mm [color="Yellow (585nm)" package="5 mm [THT]"]
  ERROR = LED - 5mm [color="Red (633nm)" package="5 mm [THT]"]
  PULSE = LED - 5mm [color="Green (555nm)" package="5 mm [THT]"]
  R7 = Resistor [resistance=220 tolerance=±5% package=THT]
  R8 = Resistor [resistance=220 tolerance=±5% package=THT]
  R9 = Resistor [resistance=220 tolerance=±5% package=THT]
  HELLO1 = LED - 5mm [color="Green (555nm)" package="5 mm [THT]"]
  R10 = Resistor [resistance=1k tolerance=±5% package=THT]
  Arduino1 = Arduino Uno (Rev3)
  ATMEGA = atmega328 [package=dip]
  XTAL = Crystal [frequency="16 Mhz" package=THT]
  C1 = Ceramic Capacitor [capacitance=22pF package="100 mil [THT, multilayer]"]
  C2 = Ceramic Capacitor [capacitance=22pF package="100 mil [THT, multilayer]"]

nets:
  N1: RESET.Pin_1, RESET.Pin_2, R10.Pin_1, Arduino1.D10_PWM/SS, ATMEGA.RESET
  GND: RESET.Pin_3, RESET.Pin_4, R6.Pin_0, R7.Pin_1, R8.Pin_1, R9.Pin_1, Arduino1.GND, ATMEGA.GND, C1.0, C2.0
  N2: R6.Pin_1, HELLO1.cathode
  N3: PROG.cathode, R9.Pin_0
  N4: PROG.anode, Arduino1.D7
  N5: ERROR.cathode, R8.Pin_0
  N6: ERROR.anode, Arduino1.D8
  N7: PULSE.cathode, R7.Pin_0
  N8: PULSE.anode, Arduino1.D9_PWM
  N9: HELLO1.anode, ATMEGA.D8
  5V: R10.Pin_0, Arduino1.5V, ATMEGA.VCC, ATMEGA.AVCC
  N10: Arduino1.D11_PWM/MOSI, ATMEGA.D11_(PWM)
  N11: Arduino1.D12/MISO, ATMEGA.D12
  N12: Arduino1.D13/SCK, ATMEGA.D13
  N13: ATMEGA.XLAT1, XTAL.pin_0, C2.1
  N14: ATMEGA.XLAT2, XTAL.pin_1, C1.1

notes:
  Using an Arduino as ISP:
  http://arduino.cc/en/Tutorial/ArduinoISP
