# Fritzing sketch 001 (saved by Fritzing 0.9.3b)
breadboards: 1

parts:
  POWER = male pin header, 8 pins [form="♂ (male)"]
  IO13 = male pin header, 10 pins [form="♂ (male)"]
  OI0 = double row male pin header, 8 pins [form="♂ (male)"]
  U1 = atmega328 [package=dip]
  U2 = attiny85 [package=dip]
  XTAL1 = Crystal [frequency="16 Mhz" package=THT]
  C1 = Ceramic Capacitor [capacitance=22pF package="100 mil [THT, multilayer]"]
  C2 = Ceramic Capacitor [capacitance=22pF package="100 mil [THT, multilayer]"]
  PROGRAMMING = LED - 5mm [color="Red (633nm)" package="5 mm [THT]"]
  ERROR = LED - 5mm [color="Red (633nm)" package="5 mm [THT]"]
  R3 = Resistor [tolerance=±5% resistance=220 package=THT]
  RUN = LED - 5mm [color="Red (633nm)" package="5 mm [THT]"]
  R4 = Resistor [tolerance=±5% resistance=220 package=THT]
  ANALOG = male pin header, 6 pins [form="♂ (male)"]  # not connected
  R2 = Resistor [tolerance=±5% resistance=220 package=THT]
  R1 = Resistor [tolerance=±5% resistance=10k package=THT]

nets (from the schematic view):
  GND: POWER.pin2, POWER.pin3, IO13.pin7, U1.GND, U2.Pin_4, C1.1, C2.1, R3.Pin_1, R4.Pin_1, R2.Pin_1
  5V: POWER.pin4, U1.VCC, U1.AVCC, U2.Pin_8, R1.Pin_0
  PD8: IO13.pin1, ERROR.anode
  PD9: IO13.pin2, RUN.anode
  PD10/SS: IO13.pin3, U1.RESET, U2.Pin_1, R1.Pin_1
  PD11/MOSI: IO13.pin4, U1.D11_(PWM), U2.Pin_5
  PD12/MISO: IO13.pin5, U1.D12, U2.Pin_6
  PD13/SCK: IO13.pin6, U1.D13, U2.Pin_7
  PD7: OI0.pin8, PROGRAMMING.anode
  OSC1: U1.XLAT1, XTAL1.pin_0, C2.0
  OSC2: U1.XLAT2, XTAL1.pin_1, C1.0
  N1: PROGRAMMING.cathode, R2.Pin_0
  N2: ERROR.cathode, R3.Pin_0
  N3: RUN.cathode, R4.Pin_0
