# Fritzing sketch V1 (saved by Fritzing 0.9.3b)
circuit board: 5.65cm x 5.33cm
breadboards: 1

parts:
  C1 = ZIF_Blue [part_number=TFXTOOL-228-3341//DS1009-28AT1NS-0A2]
  A0 = male pin header, 6 pins [form="♂ (male)"]  # not connected
  POWER = male pin header, 8 pins [form="♂ (male)"]
  SCK = LED - 3mm [color="Red (633nm)" package="3 mm [THT]"]
  D8 = male pin header, 10 pins [form="♂ (male)"]
  D0 = male pin header, 8 pins [form="♂ (male)"]
  470uf = Resistor [tolerance=±5% resistance=470 package=THT]
  470uf_2 = Resistor [tolerance=±5% resistance=470 package=THT]
  470uf_3 = Resistor [tolerance=±5% resistance=470 package=THT]
  470uf_4 = Resistor [tolerance=±5% resistance=470 package=THT]
  10K = Resistor [tolerance=±5% resistance=10k package=THT]
  ATtiny = male pin header, 2 pins [form="♂ (male)"]
  RESET = Pushbutton [package=THT]
  16MHz = Crystal [frequency="16 Mhz" package=THT]
  C1_2 = Ceramic Capacitor [capacitance=22pF package="100 mil [THT, multilayer]"]
  22pF = Ceramic Capacitor [capacitance=22pF package="100 mil [THT, multilayer]"]
  ATmega = male pin header, 3 pins [form="♂ (male)"]
  RUN = LED - 3mm [color="Red (633nm)" package="3 mm [THT]"]
  ERROR = LED - 3mm [color="Red (633nm)" package="3 mm [THT]"]
  PROG = LED - 3mm [color="Red (633nm)" package="3 mm [THT]"]
  J1 = male pin header, 2 pins [form="♂ (male)"]
  D9 = Rectifier Diode [part_number=1N4001 package="300 mil [THT]"]

nets:
  N1: C1.pin_1, D8.pin8, 10K.Pin_0, RESET.leg0, ATmega.pin1
  N2: C1.pin_7, 10K.Pin_1
  5V/GND: C1.pin_8, C1.pin_20, C1.pin_22, POWER.pin2, POWER.pin3, POWER.pin4, 470uf.Pin_1, 470uf_2.Pin_0, 470uf_3.Pin_0, 470uf_4.Pin_1, ATtiny.pin2, RESET.leg1, C1_2.0, 22pF.0, D9.cathode
  N3: C1.pin_9, ATmega.pin2
  N4: C1.pin_10, 16MHz.pin_1, C1_2.1
  N5: C1.pin_12, ATtiny.pin1
  N6: C1.pin_17, D8.pin7
  N7: C1.pin_18, D8.pin6
  N8: C1.pin_19, SCK.anode, D8.pin5
  N9: POWER.pin1, J1.pin1
  N10: SCK.cathode, 470uf.Pin_0
  N11: D8.pin9, RUN.anode
  N12: D8.pin10, ERROR.anode
  N13: D0.pin1, PROG.anode
  N14: 470uf_2.Pin_1, PROG.cathode
  N15: 470uf_3.Pin_1, RUN.cathode
  N16: 470uf_4.Pin_0, ERROR.cathode
  N17: 16MHz.pin_0, 22pF.1, ATmega.pin3
  N18: J1.pin2, D9.anode

notes:
  ATtiny
  4 3 2 1
  |

custom parts:
  ZIF_Blue: ZIF connector, 28 pin
