# Fritzing sketch b2 (saved by Fritzing 0.9.3b)
breadboards: 1

parts:
  U1 = atmega328 [package=dip]
  X1 = Crystal [frequency="16 Mhz" package=THT]
  C1 = Ceramic Capacitor [capacitance=22pF package="100 mil [THT, multilayer]"]
  C2 = Ceramic Capacitor [capacitance=22pF package="100 mil [THT, multilayer]"]
  AD = female pin header, 6 pins [form="♀ (female)"]
  IOL = female pin header, 8 pins [form="♀ (female)"]
  IOH = female pin header, 10 pins [form="♀ (female)"]
  POWER = female pin header, 8 pins [form="♀ (female)"]
  RESET_SPST = Pushbutton [package="[THT]"]
  R3 = Resistor [tolerance=±5% resistance=10k package=THT]
  C4 = Ceramic Capacitor [capacitance=100nF package="100 mil [THT, multilayer]"]
  RESET-ENC = male pin header, 2 pins [form="♂ (male)"]
  R4 = Resistor [tolerance=±5% resistance=1k package=THT]
  C5 = Ceramic Capacitor [capacitance=100nF package="100 mil [THT, multilayer]"]
  R5 = Resistor [tolerance=±5% resistance=1k package=THT]
  BLINK = LED - 5mm [color="Yellow (574nm)" package="5 mm [THT]"]
  R6 = Resistor [tolerance=±5% resistance=1k package=THT]
  R7 = Resistor [tolerance=±5% resistance=1k package=THT]
  ON = LED - 5mm [color="Green (555nm)" package="5 mm [THT]"]
  R8 = Resistor [tolerance=±5% resistance=1M package=THT]
  C6 = Ceramic Capacitor [capacitance=100nF package="100 mil [THT, multilayer]"]
  IC1 = USB UART [package=ssop28db]
  R9 = Resistor [tolerance=±5% resistance=1k package=THT]
  R10 = Resistor [tolerance=±5% resistance=1k package=THT]
  LED1 = LED - 5mm [color="Yellow (574nm)" package="5 mm [THT]"]
  LED3 = LED - 5mm [color="Red (633nm)" package="5 mm [THT]"]
  R11 = Resistor [tolerance=±5% resistance=1k package=THT]
  R12 = Resistor [tolerance=±5% resistance=1k package=THT]
  U3 = Mini-USB _B_ connector with 5th pin broken out. [package=usb-micro_b]
  F2 = Resettable Fuse PTC [package=0603]  # not connected

nets:
  ISCP/RESET: U1.RESET, POWER.pin3, RESET_SPST.Pin_3, RESET_SPST.Pin_4, R3.Pin_1, C4.0, RESET-ENC.pin1, RESET-ENC.pin2
  IO0: U1.D0_(RX), IOL.pin8, R9.Pin_1
  IO1: U1.D1_(TX), IOL.pin7, R10.Pin_1
  IO2: U1.D2, IOL.pin6
  IO3: U1.D3_(PWM), IOL.pin5
  IO4: U1.D4, IOL.pin4
  +5V: U1.VCC, U1.AVCC, POWER.pin2, POWER.pin5, R3.Pin_0, R6.Pin_0, R7.Pin_0, C6.1, R11.Pin_1, R12.Pin_1
  GND: U1.GND, C1.0, C2.0, IOH.pin4, POWER.pin6, POWER.pin7, RESET_SPST.Pin_1, RESET_SPST.Pin_2, R4.Pin_0, C5.1, BLINK.cathode, ON.cathode, C6.0, U3.GND, U3.MTN1, U3.MTN2, U3.MTN3, U3.MTN4
  N1: U1.XLAT1, X1.pin_0, C2.1, R8.Pin_0
  N2: U1.XLAT2, X1.pin_1, C1.1, R8.Pin_1
  IO5: U1.D5_(PWM), IOL.pin3
  IO6: U1.D6_(PWM), IOL.pin2
  IO7: U1.D7, IOL.pin1
  IO8: U1.D8, IOH.pin10
  IO09: U1.D9_(PWM)
  IO10/SS: U1.D10_(PWM), IOH.pin8
  IO11/MOSI: U1.D11_(PWM), IOH.pin7
  IO12/MISO: U1.D12, IOH.pin6
  IO13/SCK: U1.D13, IOH.pin5, R5.Pin_0
  AREF: U1.AREF, IOH.pin3, C5.0
  AD0: U1.A0, AD.pin6
  AD1: U1.A1, AD.pin5
  AD2: U1.A2, AD.pin4
  AD3: U1.A3, AD.pin3
  AD4/SDA: U1.A4, AD.pin2, IOH.pin2
  AD5/SCL: U1.A5, AD.pin1, IOH.pin1
  IO9: IOH.pin9
  +3V3: POWER.pin4
  VIN: POWER.pin8
  DTR: C4.1, R4.Pin_1, IC1.DTR
  N3: R5.Pin_1, BLINK.anode
  N4: R6.Pin_1, R7.Pin_1, ON.anode
  M8RXD: IC1.TXD, R9.Pin_0
  M8TXD: IC1.RXD, R10.Pin_0
  TXL: IC1.RXLED, LED3.cathode
  RXL: IC1.TXLED, LED1.cathode
  N5: LED1.anode, R11.Pin_0
  N6: LED3.anode, R12.Pin_0
