# Fritzing sketch board (saved by Fritzing 0.9.3b)
breadboards: 1

parts:
  C1 = Electrolytic Capacitor [capacitance=10µF package="100 mil [THT, electrolytic]"]
  C2 = Electrolytic Capacitor [capacitance=10µF package="100 mil [THT, electrolytic]"]
  R1 = Resistor [tolerance=±5% resistance=220 package=THT]
  Power_plug1 = Power plug
  D1 = Rectifier Diode [part_number=1N4001 package="300 mil [THT]"]
  IC1 = Voltage Regulator [package=to220-igo]
  ATMEGA = atmega328 [package=dip]
  R2 = Resistor [tolerance=±5% resistance=10k package=THT]
  XTAL1 = Crystal [frequency="16 Mhz" package=THT]
  C3 = Ceramic Capacitor [capacitance=22pF package="100 mil [THT, multilayer]"]
  C4 = Ceramic Capacitor [capacitance=22pF package="100 mil [THT, multilayer]"]
  S1 = Pushbutton [package="[THT]"]
  R3 = Resistor [tolerance=±5% resistance=220 package=THT]
  LED-ON = LED - 3mm [color="Green (555nm)" package="3 mm [THT]"]
  LED_BLINK = LED - 3mm [color="Red (633nm)" package="3 mm [THT]"]
  Componente1 = Arduino Uno (Rev3)  # not connected

nets:
  GND: C1.-, C2.-, Power_plug1.GND, IC1.GND, ATMEGA.GND, C3.0, C4.0, S1.Pin_3, S1.Pin_4, R3.Pin_1, LED-ON.cathode
  N1: C1.+, R1.Pin_1, IC1.OUT, ATMEGA.VCC, ATMEGA.AVCC, ATMEGA.AREF, R2.Pin_0
  N2: C2.+, D1.cathode, IC1.IN
  N3: R1.Pin_0, LED-ON.anode
  N4: Power_plug1.VCC, D1.anode
  N5: ATMEGA.RESET, R2.Pin_1, S1.Pin_1, S1.Pin_2
  N6: ATMEGA.XLAT1, XTAL1.pin_0, C3.1
  N7: ATMEGA.XLAT2, XTAL1.pin_1, C4.1
  N8: ATMEGA.D13, LED_BLINK.anode
  N9: R3.Pin_0, LED_BLINK.cathode
