# Fritzing sketch board2.2 (saved by Fritzing 0.9.3b)
breadboards: 1

parts:
  C5 = Electrolytic Capacitor [capacitance=10µF package="100 mil [THT, electrolytic]"]
  R5 = Resistor [tolerance=±5% resistance=220 package=THT]
  Power_plug2 = Power plug
  IC2 = Voltage Regulator [package=to220-igo]
  D2 = Rectifier Diode [part_number=1N4001 package="300 mil [THT]"]
  C6 = Electrolytic Capacitor [capacitance=10µF package="100 mil [THT, electrolytic]"]
  Componente1 = Arduino Uno (Rev3)-TopMount  # not connected
  ATMEGA328P-PU = atmega328 [package=dip]
  C9 = Ceramic Capacitor [capacitance=100nF package="100 mil [THT, multilayer]"]
  LED-ON1 = LED - 3mm [color="Green (555nm)" package="3 mm [THT]"]
  R6 = Resistor [tolerance=±5% resistance=1M package=THT]
  XTAL1 = Crystal [frequency="16 Mhz" package=THT]
  C10 = Ceramic Capacitor [capacitance=22pF package="100 mil [THT, multilayer]"]
  C11 = Ceramic Capacitor [capacitance=22pF package="100 mil [THT, multilayer]"]
  D3 = Rectifier Diode [part_number=1N4001 package="300 mil [THT]"]
  R7 = Resistor [tolerance=±5% resistance=10k package=THT]
  POWER = female pin header, 8 pins [form="♀ (female)"]
  J2 = male pin header, 2 pins [form="♂ (male)"]
  C12 = Ceramic Capacitor [capacitance=100nF package="100 mil [THT, multilayer]"]
  R8 = Resistor [tolerance=±5% resistance=1k package=THT]

nets:
  GND: C5.-, Power_plug2.GND, IC2.GND, C6.-, ATMEGA328P-PU.GND, C9.0, LED-ON1.cathode, C10.0, C11.0, POWER.pin6, POWER.pin7, R8.Pin_1
  N1: C5.+, IC2.IN, D2.cathode
  N2: R5.Pin_0, LED-ON1.anode
  5V: R5.Pin_1, IC2.OUT, C6.+, ATMEGA328P-PU.VCC, ATMEGA328P-PU.AVCC, C9.1, D3.cathode, R7.Pin_1, POWER.pin2, POWER.pin5
  N3: Power_plug2.VCC, D2.anode
  RESET: ATMEGA328P-PU.RESET, D3.anode, R7.Pin_0, POWER.pin3, J2.pin1, J2.pin2, C12.1
  N4: ATMEGA328P-PU.XLAT1, R6.Pin_0, XTAL1.pin_0, C10.1
  N5: ATMEGA328P-PU.XLAT2, R6.Pin_1, XTAL1.pin_1, C11.1
  AREF: ATMEGA328P-PU.AREF
  3.3V: POWER.pin4
  VIN: POWER.pin8
  DTR: C12.0, R8.Pin_0

custom parts:
  Arduino Uno (Rev3)-TopMount: Arduino Uno (Rev3) for Top PCB Mount. The PCB view of the Arduino Uno (Rev3) in Arduino Bin flipped upside down with the text flipped back so as to be readable. Other views haven't changed Protruding component position is outlined to provide indication of part contact. Number in component outline is mm of protrusion of the component from the UNO PCB. Subtract the number from the USB (11mm),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
