# Fritzing sketch board2 (saved by Fritzing 0.9.3b)
circuit board: 6.85226cm x 5.31026cm
breadboards: 1

parts:
  C5 = Electrolytic Capacitor [capacitance=10µF package="100 mil [THT, electrolytic]"]
  R4 = Resistor [tolerance=±5% resistance=10k package=THT]
  R5 = Resistor [tolerance=±5% resistance=220 package=THT]
  LED-ON1 = LED - 3mm [color="Green (555nm)" package="3 mm [THT]"]
  Power_plug2 = Power plug
  IC2 = Voltage Regulator [package=to220-igo]
  D2 = Rectifier Diode [part_number=1N4001 package="300 mil [THT]"]
  ATMEGA1 = atmega328 [package=dip]
  XTAL2 = Crystal [frequency="16 Mhz" package=THT]
  C7 = Ceramic Capacitor [capacitance=22pF package="100 mil [THT, multilayer]"]
  C8 = Ceramic Capacitor [capacitance=22pF package="100 mil [THT, multilayer]"]
  S2 = Pushbutton [package="[THT]"]
  R6 = Resistor [tolerance=±5% resistance=220 package=THT]
  LED_BLINK1 = LED - 3mm [color="Red (633nm)" package="3 mm [THT]"]
  C6 = Electrolytic Capacitor [capacitance=10µF package="100 mil [THT, electrolytic]"]
  Componente1 = Arduino Uno (Rev3)-TopMount  # not connected
  ANALOG = female pin header, 6 pins [form="♀ (female)"]
  PO_WER = female pin header, 6 pins [form="♀ (female)"]  # not connected
  ATMEGA328P-PU = atmega328 [package=dip]
  C9 = Ceramic Capacitor [capacitance=100nF package="100 mil [THT, multilayer]"]

nets:
  GND: C5.-, LED-ON1.cathode, Power_plug2.GND, IC2.GND, ATMEGA1.GND, C7.0, C8.0, S2.Pin_3, S2.Pin_4, R6.Pin_1, C6.-, ATMEGA328P-PU.GND, C9.0
  N1: C5.+, IC2.IN, D2.cathode
  5V: R4.Pin_0, R5.Pin_1, IC2.OUT, ATMEGA1.VCC, ATMEGA1.AVCC, ATMEGA1.AREF, C6.+, ATMEGA328P-PU.VCC, ATMEGA328P-PU.AVCC, C9.1
  N2: R4.Pin_1, ATMEGA1.RESET, S2.Pin_1, S2.Pin_2
  N3: R5.Pin_0, LED-ON1.anode
  N4: Power_plug2.VCC, D2.anode
  N5: ATMEGA1.XLAT1, XTAL2.pin_0, C7.1
  N6: ATMEGA1.XLAT2, XTAL2.pin_1, C8.1
  N7: ATMEGA1.D13, LED_BLINK1.anode
  N8: ATMEGA1.A0, ANALOG.pin6
  N9: ATMEGA1.A1, ANALOG.pin5
  N10: ATMEGA1.A2, ANALOG.pin4
  N11: ATMEGA1.A3, ANALOG.pin3
  N12: ATMEGA1.A4, ANALOG.pin2
  N13: ATMEGA1.A5, ANALOG.pin1
  N14: R6.Pin_0, LED_BLINK1.cathode

custom parts:
  Arduino Uno (Rev3)-TopMount: Arduino Uno (Rev3) for Top PCB Mount. The PCB view of the Arduino Uno (Rev3) in Arduino Bin flipped upside down with the text flipped back so as to be readable. Other views haven't changed Protruding component position is outlined to provide indication of part contact. Number in component outline is mm of protrusion of the component from the UNO PCB. Subtract the number from the USB (11mm),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
