# Fritzing sketch board3 (saved by Fritzing 0.9.3b)

parts:
  C5 = Electrolytic Capacitor [capacitance=10µF package="100 mil [THT, electrolytic]"]
  R5 = Resistor [tolerance=±5% resistance=220 package=THT]
  Power_plug2 = Power plug
  IC2 = Voltage Regulator [package=to220-igo]
  D2 = Rectifier Diode [part_number=1N4001 package="300 mil [THT]"]
  C6 = Electrolytic Capacitor [capacitance=10µF package="100 mil [THT, electrolytic]"]
  Componente1 = Arduino Uno (Rev3)-TopMount  # not connected
  LED-ON1 = LED - 3mm [color="Green (555nm)" package="3 mm [THT]"]
  U3 = USB UART [package=ssop28db]
  LED1 = LED - 5mm [color="Red (633nm)" package="5 mm [THT]"]
  R6 = Resistor [tolerance=±5% resistance=200 package=THT]
  X1 = Crystal [frequency="16 Mhz" package=THT]
  C7 = Ceramic Capacitor [capacitance=22pF package="100 mil [THT, multilayer]"]
  C8 = Ceramic Capacitor [capacitance=22pF package="100 mil [THT, multilayer]"]
  S1 = Pushbutton [package="[THT]"]
  R7 = Resistor [tolerance=±5% resistance=10k package=THT]
  C9 = Ceramic Capacitor [capacitance=0.1µF package="100 mil [THT, multilayer]"]
  PWR = female pin header, 8 pins [form="♀ (female)"]
  A0-A1 = female pin header, 6 pins [form="♀ (female)"]
  U4 = atmega328 [package=dip]
  0-7 = male pin header, 8 pins [form="♂ (male)"]
  8-13 = female pin header, 10 pins [form="♀ (female)"]
  C10 = Ceramic Capacitor [capacitance=100nF package="100 mil [THT, multilayer]"]
  X2 = Mini-USB _B_ connector with 5th pin broken out. [package=usb-minib]

nets:
  GND: C5.-, Power_plug2.GND, IC2.GND, C6.-, LED-ON1.cathode, U3.GND1, U3.GND2, U3.GND3, U3.AGND, U3.TEST, R6.Pin_1, C7.0, C8.0, S1.Pin_3, S1.Pin_4, PWR.pin2, PWR.pin3, U4.GND, 8-13.pin4, C10.0, X2.MTN2, X2.MTN3, X2.MTN1, X2.MTN4, X2.GND
  N1: C5.+, IC2.IN, D2.cathode
  N2: R5.Pin_0, LED-ON1.anode
  5V: R5.Pin_1, IC2.OUT, C6.+, R7.Pin_0, PWR.pin4, PWR.pin7, U4.VCC, U4.AVCC, U4.AREF, 8-13.pin3
  N3: Power_plug2.VCC, D2.anode
  N4: U3.USBDP, X2.D+
  N5: U3.USBDM, X2.D-
  N6: LED1.cathode, R6.Pin_0
  D13: LED1.anode, U4.D13, 8-13.pin5
  N7: X1.pin_0, C7.1, U4.XLAT1
  N8: X1.pin_1, C8.1, U4.XLAT2
  N9: S1.Pin_1, S1.Pin_2, R7.Pin_1, C9.1, U4.RESET
  DTR: C9.0
  Vin: PWR.pin1
  3.3V: PWR.pin5
  Reset: PWR.pin6
  A5: A0-A1.pin1, U4.A5, 8-13.pin1
  A4: A0-A1.pin2, U4.A4, 8-13.pin2
  A3: A0-A1.pin3, U4.A3
  A2: A0-A1.pin4, U4.A2
  A1: A0-A1.pin5, U4.A1
  A0: A0-A1.pin6, U4.A0
  M8TX/Rx: U4.D0_(RX), 0-7.pin8
  M8RX/Tx: U4.D1_(TX), 0-7.pin7
  D2: U4.D2, 0-7.pin6
  D3: U4.D3_(PWM), 0-7.pin5
  D4: U4.D4, 0-7.pin4
  D5: U4.D5_(PWM), 0-7.pin3
  D6: U4.D6_(PWM), 0-7.pin2
  D7: U4.D7, 0-7.pin1
  D8: U4.D8, 8-13.pin10
  D9: U4.D9_(PWM), 8-13.pin9
  D10: U4.D10_(PWM), 8-13.pin8
  D11: U4.D11_(PWM), 8-13.pin7
  D12: U4.D12, 8-13.pin6

custom parts:
  Arduino Uno (Rev3)-TopMount: Arduino Uno (Rev3) for Top PCB Mount. The PCB view of the Arduino Uno (Rev3) in Arduino Bin flipped upside down with the text flipped back so as to be readable. Other views haven't changed Protruding component position is outlined to provide indication of part contact. Number in component outline is mm of protrusion of the component from the UNO PCB. Subtract the number from the USB (11mm),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
