# Fritzing sketch V1.1 (saved by Fritzing 0.9.3b)
circuit board: 9cm x 6cm

parts:
  ON = LED - 3mm [color="Red (633nm)" package="3 mm [THT]"]
  -_1K_- = Resistor [tolerance=±5% resistance=1k package=THT]
  22pF = Capacitor [package=cap-pth-small-kit]
  0_1uF = Ceramic Capacitor [capacitance=100nF package="100 mil [THT, multilayer]"]
  +_- = Rectifier Diode [part_number=1N4001 package="300 mil [THT]"]
  -_10K_- = Resistor [tolerance=±5% resistance=10k package=THT]
  22pF_2 = Capacitor [package=cap-pth-small-kit]
  -_100K_- = Resistor [tolerance=±5% resistance=100k package=THT]
  16Mhz = Crystal [frequency="16 Mhz" package=THT]
  +_-_2 = Rectifier Diode [part_number=1N4001 package="300 mil [THT]"]
  Atmega328P = atmega328 [package=dip]
  IN = female pin header, 2 pins [form="♀ (female)"]
  -_1K_-_2 = Resistor [tolerance=±5% resistance=1k package=THT]
  USB-Serial = female pin header, 5 pins [form="♀ (female)"]
  5_•_6_•_7_•_8 = female pin header, 4 pins [form="♀ (female)"]
  LDR = female pin header, 2 pins [form="♀ (female)"]
  Bluetooth = female pin header, 6 pins [form="♀ (female)"]
  •A5_•A4_•A3_•A2_•A1_•A0 = female pin header, 6 pins [form="♀ (female)"]
  13 = LED - 3mm [color="Red (633nm)" package="3 mm [THT]"]
  PW12 = Power Jack [package=power_jack_pth_lock]
  -_+ = Rectifier Diode [part_number=1N4001 package="300 mil [THT]"]
  U1 = Voltage Regulator -- 3.3 V -- LM1117
  47µF = Electrolytic Capacitor [capacitance=47µF package="100 mil [THT, electrolytic]"]
  47uF = Electrolytic Capacitor [capacitance=47µF package="100 mil [THT, electrolytic]"]
  100nF = Ceramic Capacitor [capacitance=100nF package="100 mil [THT, multilayer]"]
  USBIN = USB Connectors [package=usb-a-h]
  RST•_0•_1•_2•_3_•_4 = female pin header, 6 pins [form="♀ (female)"]
  S1 = Pushbutton [package="[THT]"]
  -_10K_-_2 = Resistor [tolerance=±5% resistance=10k package=THT]
  •13_•12_•11_•10_•9_•8 = female pin header, 6 pins [form="♀ (female)"]
  DHT22 = female pin header, 3 pins [form="♀ (female)"]
  Moisture = USB Connectors [package=usb-a-h]
  WaterLevel = USB Connectors [package=usb-a-h]

nets:
  N1: ON.cathode, -_1K_-.Pin_1
  5V: ON.anode, +_-.cathode, -_10K_-.Pin_0, -_100K_-.Pin_0, +_-_2.cathode, Atmega328P.VCC, Atmega328P.AVCC, Atmega328P.AREF, -_10K_-_2.Pin_0, DHT22.pin1, Moisture.VBUS, WaterLevel.VBUS
  GND: -_1K_-.Pin_0, 22pF.1, 22pF_2.1, Atmega328P.GND, IN.pin2, USB-Serial.pin1, LDR.pin2, Bluetooth.pin3, 13.cathode, PW12.GND, PW12.GNDBREAK, U1.GND, 47µF.-, 47uF.-, 100nF.0, USBIN.GND, S1.Pin_3, S1.Pin_4, DHT22.pin3, Moisture.GND, WaterLevel.GND
  N2: 22pF.2, 16Mhz.pin_1, Atmega328P.XLAT2
  N3: 0_1uF.0, -_10K_-.Pin_1, Atmega328P.D0_(RX), USB-Serial.pin3, RST•_0•_1•_2•_3_•_4.pin2
  N4: 0_1uF.1, USB-Serial.pin5
  N5: +_-.anode, USB-Serial.pin2
  N6: 22pF_2.2, 16Mhz.pin_0, Atmega328P.XLAT1
  N7: -_100K_-.Pin_1, LDR.pin1
  5V VCC: +_-_2.anode, IN.pin1, U1.OUT, 47uF.+, 100nF.1, USBIN.VBUS
  N8: Atmega328P.RESET, RST•_0•_1•_2•_3_•_4.pin1, S1.Pin_1, S1.Pin_2, -_10K_-_2.Pin_1
  N9: Atmega328P.D1_(TX), USB-Serial.pin4, RST•_0•_1•_2•_3_•_4.pin3
  N10: Atmega328P.D2, RST•_0•_1•_2•_3_•_4.pin4, DHT22.pin2
  N11: Atmega328P.D3_(PWM), Bluetooth.pin2, RST•_0•_1•_2•_3_•_4.pin5
  N12: Atmega328P.D4, Bluetooth.pin1, RST•_0•_1•_2•_3_•_4.pin6
  N13: Atmega328P.D5_(PWM), 5_•_6_•_7_•_8.pin1, Bluetooth.pin4
  N14: Atmega328P.D6_(PWM), 5_•_6_•_7_•_8.pin2, Bluetooth.pin5
  N15: Atmega328P.D7, 5_•_6_•_7_•_8.pin3
  N16: Atmega328P.D8, 5_•_6_•_7_•_8.pin4, •13_•12_•11_•10_•9_•8.pin6
  N17: Atmega328P.D9_(PWM), •13_•12_•11_•10_•9_•8.pin5
  N18: Atmega328P.D10_(PWM), •13_•12_•11_•10_•9_•8.pin4
  N19: Atmega328P.D11_(PWM), •13_•12_•11_•10_•9_•8.pin3
  N20: Atmega328P.D12, •13_•12_•11_•10_•9_•8.pin2
  N21: Atmega328P.D13, -_1K_-_2.Pin_0, •13_•12_•11_•10_•9_•8.pin1
  N22: Atmega328P.A0, •A5_•A4_•A3_•A2_•A1_•A0.pin6, Moisture.D+
  N23: Atmega328P.A1, •A5_•A4_•A3_•A2_•A1_•A0.pin5, WaterLevel.D+
  N24: Atmega328P.A2, •A5_•A4_•A3_•A2_•A1_•A0.pin4
  N25: Atmega328P.A3, •A5_•A4_•A3_•A2_•A1_•A0.pin3
  N26: Atmega328P.A4, •A5_•A4_•A3_•A2_•A1_•A0.pin2
  N27: Atmega328P.A5, •A5_•A4_•A3_•A2_•A1_•A0.pin1
  N28: -_1K_-_2.Pin_1, 13.anode
  N29: PW12.PWR, -_+.anode
  12V: -_+.cathode, U1.IN, 47µF.+

notes:
  5V GND TX RX
  SDA
  SCL
  RX TX
  GND +V  TX RX DTR
  EN VCC GND TX RX  ST
  GND

custom parts:
  Voltage Regulator -- 3.3 V -- LM1117: LM1117-3.3 Voltage regulator, 3.3 V output. Note that the pinout order is not the same as LM7805 or LM7833.
