# Fritzing sketch v2 (saved by Fritzing 0.9.3b)
breadboards: 1

parts:
  IC1 = atmega328 [package=dip]
  X1 = Crystal [frequency="16 Mhz" package=THT]
  C00 = Ceramic Capacitor [capacitance=22pF package="100 mil [THT, multilayer]"]
  C0 = Ceramic Capacitor [capacitance=22pF package="100 mil [THT, multilayer]"]
  R1 = Resistor [tolerance=±5% resistance=10k package=THT]
  S1 = Pushbutton [package="[THT]"]
  C6 = Electrolytic Capacitor [capacitance=0.1µF package="100 mil [THT, electrolytic]"]
  C2 = Electrolytic Capacitor [capacitance=0.1µF package="100 mil [THT, electrolytic]"]
  J1 = Power Jack [package=power_jack_pth]
  D1 = Rectifier Diode [part_number=1N4001 package="300 mil [THT]"]
  C1 = Electrolytic Capacitor [capacitance=0.1µF package="100 mil [THT, electrolytic]"]
  C3 = Electrolytic Capacitor [capacitance=10µF voltage=25V package="100 mil [THT, electrolytic]"]
  IC2 = Voltage Regulator [package=to-220-alt]
  C4 = Electrolytic Capacitor [capacitance=100µF voltage=6V package="100 mil [THT, electrolytic]"]
  C5 = Electrolytic Capacitor [capacitance=0.1µF package="100 mil [THT, electrolytic]"]
  JP4 = female pin header, 4 pins [form="♀ (female)"]
  JP3 = double row female pin header, 6 pins [form="♀ (female)"]
  R3 = Resistor [tolerance=±5% resistance=1k package=THT]
  D3 = LED - 5mm [color="Red (635nm)" package="5 mm [THT]"]
  J2 = female pin header, 3 pins [form="♀ (female)"]
  R2 = Resistor [tolerance=±5% resistance=1.0k package=THT]
  LED1 = LED - 3mm [color="Red (633nm)" package="3 mm [THT]"]
  JA1 = female pin header, 6 pins [form="♀ (female)"]
  JD1 = female pin header, 8 pins [form="♀ (female)"]
  JD2 = female pin header, 8 pins [form="♀ (female)"]

nets:
  RST: IC1.RESET, R1.Pin_1, S1.Pin_3, S1.Pin_4, C6.-, JP4.pin4, JP3.pin6
  N1: IC1.D0_(RX), JD1.pin1
  N2: IC1.D1_(TX), JD1.pin2
  N3: IC1.D2, JD1.pin3
  N4: IC1.D3_(PWM), JD1.pin4
  N5: IC1.D4, JD1.pin5
  +5V: IC1.VCC, IC1.AVCC, R1.Pin_0, C2.+, JP4.pin1, JP3.pin3, J2.pin2, R2.Pin_1
  GND: IC1.GND, C00.0, C0.0, S1.Pin_1, S1.Pin_2, C2.-, J1.GND, C1.-, C3.-, IC2.GND, C4.-, C5.-, JP4.pin2, JP3.pin1, D3.cathode, LED1.cathode
  N6: IC1.XLAT1, X1.pin_0, C00.1
  N7: IC1.XLAT2, X1.pin_1, C0.1
  N8: IC1.D5_(PWM), JD1.pin6
  N9: IC1.D6_(PWM), JD1.pin7
  N10: IC1.D7, JD1.pin8
  N11: IC1.D8, JD2.pin1
  N12: IC1.D9_(PWM), JD2.pin2
  N13: IC1.D10_(PWM), JD2.pin3
  AREF: IC1.AREF
  N14: IC1.A0, JA1.pin1
  N15: IC1.A1, JA1.pin2
  N16: IC1.A2, JA1.pin3
  N17: IC1.A3, JA1.pin4
  N18: IC1.A4, JA1.pin5
  N19: IC1.A5, JA1.pin6
  RTS#: C6.+
  N20: J1.PWR, D1.anode
  +9V: D1.cathode, C1.+, C3.+, IC2.IN, JP4.pin3
  N21: IC2.OUT, C4.+, C5.+, J2.pin1
  MOSI: JP3.pin2
  MISO: JP3.pin4, R3.Pin_1
  SCK: JP3.pin5
  N22: R3.Pin_0, D3.anode
  USB_5V: J2.pin3
  N23: R2.Pin_0, LED1.anode
