# Fritzing sketch DIY Arduino ark (saved by Fritzing 0.9.3b)
breadboards: 1

parts:
  R1 = Resistor [resistance=220 tolerance=±5% package=THT]
  J1 = female pin header, 2 pins [form="♀ (female)"]
  J2 = female pin header, 2 pins [form="♀ (female)"]
  J3 = female pin header, 2 pins [form="♀ (female)"]
  J4 = female pin header, 2 pins [form="♀ (female)"]
  J5 = female pin header, 2 pins [form="♀ (female)"]
  J6 = female pin header, 2 pins [form="♀ (female)"]
  J7 = female pin header, 2 pins [form="♀ (female)"]
  J8 = female pin header, 2 pins [form="♀ (female)"]
  J9 = female pin header, 2 pins [form="♀ (female)"]
  J10 = female pin header, 2 pins [form="♀ (female)"]
  J11 = female pin header, 2 pins [form="♀ (female)"]
  Power = Screw terminal - 2 pins [package=THT]
  U1 = atmega168 [package=dip]
  C2 = Ceramic Capacitor [capacitance=100nF package="100 mil [THT, multilayer]"]
  C1 = Ceramic Capacitor [capacitance=100nF package="100 mil [THT, multilayer]"]
  XTAL1 = Crystal [frequency="16 Mhz" package=THT]
  J12 = female pin header, 1 pin [form="♀ (female)"]
  Power_plug1 = Power plug

nets:
  N1: R1.Pin_0, J7.pin1, U1.VCC
  N2: R1.Pin_1, J4.pin1, U1.RESET
  N3: J1.pin1, U1.A5
  N4: J1.pin2, U1.A4
  N5: J2.pin1, U1.A3
  N6: J2.pin2, U1.A2
  N7: J3.pin1, U1.A1
  N8: J3.pin2, U1.A0
  N9: J4.pin2, U1.D0_(RX)
  N10: J5.pin1, U1.D1_(TX)
  N11: J5.pin2, U1.D2
  N12: J6.pin1, U1.D3_(PWM)
  N13: J6.pin2, U1.D4
  N14: J7.pin2, U1.GND#7, C2.0, C1.0
  N15: J8.pin1, U1.D5_(PWM)
  N16: J8.pin2, U1.D6_(PWM)
  N17: J9.pin1, U1.D7
  N18: J9.pin2, U1.D8
  N19: J10.pin1, U1.D10_(PWM)
  N20: J10.pin2, U1.D9_(PWM)
  N21: J11.pin1, U1.D12
  N22: J11.pin2, U1.D11_(PWM)
  N23: Power.pin1, U1.GND#21, Power_plug1.GND
  N24: Power.pin2, U1.AVCC, Power_plug1.VCC
  N25: U1.XLAT1, C1.1, XTAL1.pin_0
  N26: U1.XLAT2, C2.1, XTAL1.pin_1
  N27: U1.D13, J12.pin1

notes:
  ##
