# Fritzing sketch SISPRA-MD-001-V-2-0-0 (saved by Fritzing 0.9.3b)
breadboards: 3
perfboards: 7

parts:
  Componente1 = Arduino Uno (Rev3)
  Tiny_RTC1 = Tiny RTC
  Componente2 = DHT22 Module FG
  Componente4 = Bluetooth HC-05 Macho
  Componente5 = Arduino Uno (Rev3)
  R1 = Resistor [tolerance=±5% resistance=220 package=THT]  # not connected
  Tiny_RTC3 = Tiny RTC
  Componente8 = Bluetooth HC-05 Macho
  Componente9 = DHT22 Module FG
  Componente10 = Arduino Uno (Rev3)
  LED1 = LED - 5mm [color="Red (635nm)" package="5 mm [THT]"]
  LED3 = LED - 5mm [color="Green (555nm)" package="5 mm [THT]"]
  R2 = Resistor [tolerance=±5% resistance=220 package=THT]
  R3 = Resistor [tolerance=±5% resistance=220 package=THT]
  Componente11 = FC-28 Soil Hygrometer Module  # not connected
  Componente12 = Arduino Uno (Rev3)  # not connected
  Componente13 = FC-28 Soil Hygrometer Module  # not connected
  R6 = Resistor [tolerance=±5% resistance=220 package=THT]
  LED4 = LED - 5mm [color="Green (555nm)" package="5 mm [THT]"]
  R7 = Resistor [tolerance=±5% resistance=220 package=THT]
  LED5 = LED - 5mm [color="Red (635nm)" package="5 mm [THT]"]
  Componente14 = DHT22 Module FG  # not connected
  Componente15 = Bluetooth HC-05 Macho  # not connected

nets:
  GND: Componente1.GND, Tiny_RTC1.GND, Componente2.GND, Componente4.GND
  N1: Componente1.A4/SDA, Tiny_RTC1.SDA
  N2: Componente1.A5/SCL, Tiny_RTC1.SCL
  N3: Componente1.D2, Componente2.OUT
  N4: Componente1.D3_PWM, Componente4.VCC
  N5: Componente1.D4, Componente4.Key
  N6: Componente1.D5_PWM, Componente4.TXD
  N7: Componente1.D6_PWM, Componente4.RXD
  VCC: Componente1.5V, Tiny_RTC1.VCC, Componente2.VCC
  N8: Componente5.A4/SDA, Tiny_RTC3.SDA, Componente10.A4/SDA
  N9: Componente5.A5/SCL, Tiny_RTC3.SCL, Componente10.A5/SCL
  GND_2: Componente5.GND, Tiny_RTC3.GND, Componente8.GND, Componente9.GND, Componente10.GND, R2.Pin_1, R3.Pin_1
  N10: Componente5.D2, Componente9.OUT
  N11: Componente5.D4, Componente8.Key
  N12: Componente5.D5_PWM, Componente8.TXD
  N13: Componente5.D6_PWM, Componente8.RXD
  VCC_2: Componente5.5V, Tiny_RTC3.VCC, Componente9.VCC
  N14: Componente10.D2, LED3.anode
  N15: Componente10.D3_PWM, LED1.anode
  N16: LED1.cathode, R3.Pin_0
  N17: LED3.cathode, R2.Pin_0
  N18: R6.Pin_0, LED4.cathode
  N19: R6.Pin_1, R7.Pin_1
  N20: R7.Pin_0, LED5.cathode

custom parts:
  Tiny RTC: Tiny RTC I2C module DS1370Z RTC and AT24C32 EEPROM
  DHT22 Module FG: DHT22 module
  FC-28 Soil Hygrometer Module: The FC-28 is a soil hygrometer module that uses the Texas Instruments LM393 comparator chip to provide an analog measurement of soil humidity. The digital output is high when soil moisture is over a certain threshold, as determined by adjusting the potentiometer.

// code stored in the sketch: 1_0_0.ino
/* 
#########################################################
#    Processor:          Arduino UNO, MEGA ou Teensy++ 2.0
#    Language:           Wiring / C /Processing /Fritzing / Arduino IDE
#    Objectives:         Test Module - Tiny RTC DS1307 Z
#    Author:             Andres Felipe Gomez Maya
#    Date:               17/10/2019
#    place:              Medellin, Colombia
#########################################################
#  
#  RTC-I2C: DS:SCL->ARD:SCL  DS:SDA->ARD:SDA  DS:VCC->5V  DS:GND->GND
#           **NOTA**: se debe cargar dos veces este programa 1.Con la linea 9= RTC.adjust(DateTime(__DATE__, __TIME__));
#    
#    
#    
#    
*/

#include <Wire.h> 
#include "RTClib.h"
RTC_DS1307 RTC;
#define A0 A0

void setup () {
  Serial.begin(9600); // Establece la velocidad de datos del puerto serie
  Serial.println("Iniciando el puerto I2C");
  Wire.begin();  
  Serial.println("Abriendo Wire.");.

  if (! RTC.begin()) {
    Serial.println("RTC No Encontrado.");
    while (1);
  }

  if (! RTC.isrunning()) {
    Serial.println("RTC NO funciona!");
  }
  
  // RTC.adjust(DateTime(__DATE__, __TIME__)); // Establece la fecha y hora (Comentar una vez establecida la hora)
} 


void loop(){

  if (! RTC.isrunning()) {
    Serial.println("RTC NO funciona!");
  } else {
    DateTime now = RTC.now(); // Obtiene la fecha y hora del   RTC
    Serial.print(now.year(), DEC); // A§o
    Serial.print('/');
    Serial.print(now.month(), DEC); // Mes
    Serial.print('/');
    Serial.print(now.day(), DEC); // Dia
    Serial.print(' ');
    Serial.print(now.hour(), DEC); // Horas
    Serial.print(':');
    Serial.print(now.minute(), DEC); // Minutos
    Serial.print(':');
    Serial.print(now.second(), DEC); // Segundos
    Serial.println();
  }
}

// code stored in the sketch: test_ds1307z_0.ino
/* 
#########################################################
#    Processor:          Arduino UNO, MEGA ou Teensy++ 2.0
#    Language:           Wiring / C /Processing /Fritzing / Arduino IDE
#    Objectives:         Test Module - Tiny RTC DS1307 Z
#    Author:             Andres Felipe Gomez Maya
#    Date:               17/10/2019
#    place:              Medellin, Colombia
#########################################################
*/

//  Prueba de Reloj Tiempo Real (RTC) y Modulo I2C
//  Conexion:
//    Arduino UNO  SCL->SCL  SDA->SDA  VCC->5V  GND->GND
//  
//    NOTA: se debe cargar dos veces este programa 1.Con la linea 9= RTC.adjust(DateTime(__DATE__, __TIME__));

#include <Wire.h> 
#include "RTClib.h"
RTC_DS1307 RTC;

void setup () {
  Serial.begin(9600); // Establece la velocidad de datos del puerto serie
  Serial.println("Inicia el puerto I2C");
  
  Serial.println("Abriendo Wire.");
  Wire.begin(); // 
  
  Serial.println("RTC Begin.");
  RTC.begin(); // Inicia la comunicaci?n con el RTC
  // RTC.adjust(DateTime(__DATE__, __TIME__)); // Establece la fecha y hora (Comentar una vez establecida la hora)
}
void loop(){
  DateTime now = RTC.now(); // Obtiene la fecha y hora del RTC
  Serial.print(now.year(), DEC); // A?o
  Serial.print('/');
  Serial.print(now.month(), DEC); // Mes
  Serial.print('/');
  Serial.print(now.day(), DEC); // Dia
  Serial.print(' ');
  Serial.print(now.hour(), DEC); // Horas
  Serial.print(':');
  Serial.print(now.minute(), DEC); // Minutos
  Serial.print(':');
  Serial.print(now.second(), DEC); // Segundos
  Serial.println();
}
